// Digital circuit ALU.dig as structural Verilog
module ALU (
  input  in_1,
  input  in_2,
  input  in_3,
  input  in_4,
  input  in_5,
  input  in_6,
  input  in_7,
  input  in_8,
  input  in_9,
  input  in_10,
  input  in_11,
  output out_12,
  output out_13,
  output out_14,
  output out_15,
  output out_16,
  output out_17
);

  wire add_1_c_o, add_1_s, add_2_c_o, add_2_s, add_3_c_o, add_3_s, add_4_s, and_1_out, and_2_out, and_3_out,
       and_4_out, or_1_out, or_2_out, or_3_out, or_4_out, sub_1_c_o, sub_1_s, sub_2_c_o, sub_2_s, sub_3_c_o,
       sub_3_s, sub_4_s, xor_1_out, xor_2_out, xor_3_out, xor_4_out;

  Sub sub_1 (.a(in_1), .b(in_5), .c_i(1'b0), .s(sub_1_s), .c_o(sub_1_c_o));
  Sub sub_2 (.a(in_2), .b(in_6), .c_i(sub_1_c_o), .s(sub_2_s), .c_o(sub_2_c_o));
  Sub sub_3 (.a(in_3), .b(in_7), .c_i(sub_2_c_o), .s(sub_3_s), .c_o(sub_3_c_o));
  Sub sub_4 (.a(in_4), .b(in_8), .c_i(sub_3_c_o), .s(sub_4_s), .c_o(out_17));
  Add add_1 (.a(in_1), .b(in_5), .c_i(1'b0), .s(add_1_s), .c_o(add_1_c_o));
  Add add_2 (.a(in_2), .b(in_6), .c_i(add_1_c_o), .s(add_2_s), .c_o(add_2_c_o));
  Add add_3 (.a(in_3), .b(in_7), .c_i(add_2_c_o), .s(add_3_s), .c_o(add_3_c_o));
  Add add_4 (.a(in_4), .b(in_8), .c_i(add_3_c_o), .s(add_4_s), .c_o(out_16));
  and and_1 (and_1_out, in_1, in_5);
  and and_2 (and_2_out, in_2, in_6);
  and and_3 (and_3_out, in_3, in_7);
  and and_4 (and_4_out, in_4, in_8);
  or or_1 (or_1_out, in_1, in_5);
  or or_2 (or_2_out, in_2, in_6);
  or or_3 (or_3_out, in_3, in_7);
  or or_4 (or_4_out, in_4, in_8);
  xor xor_1 (xor_1_out, in_1, in_5);
  xor xor_2 (xor_2_out, in_2, in_6);
  xor xor_3 (xor_3_out, in_3, in_7);
  xor xor_4 (xor_4_out, in_4, in_8);
  Multiplexer #(.Selector_Bits(3)) multiplexer_1 (
    .sel({in_11, in_10, in_9}), .in_0(sub_1_s), .in_1(add_1_s), .in_2(and_1_out), .in_3(or_1_out),
    .in_4(xor_1_out), .in_5(1'b0), .in_6(1'b0), .in_7(1'b0), .out(out_12));
  Multiplexer #(.Selector_Bits(3)) multiplexer_2 (
    .sel({in_11, in_10, in_9}), .in_0(sub_2_s), .in_1(add_2_s), .in_2(and_2_out), .in_3(or_2_out),
    .in_4(xor_2_out), .in_5(1'b0), .in_6(1'b0), .in_7(1'b0), .out(out_13));
  Multiplexer #(.Selector_Bits(3)) multiplexer_3 (
    .sel({in_11, in_10, in_9}), .in_0(sub_3_s), .in_1(add_3_s), .in_2(and_3_out), .in_3(or_3_out),
    .in_4(xor_3_out), .in_5(1'b0), .in_6(1'b0), .in_7(1'b0), .out(out_14));
  Multiplexer #(.Selector_Bits(3)) multiplexer_4 (
    .sel({in_11, in_10, in_9}), .in_0(sub_4_s), .in_1(add_4_s), .in_2(and_4_out), .in_3(or_4_out),
    .in_4(xor_4_out), .in_5(1'b0), .in_6(1'b0), .in_7(1'b0), .out(out_15));
endmodule
