// Digital circuit cpu.dig as structural Verilog
module cpu (
  input  in_1,
  input  in_2,
  input  in_3,
  input  in_4,
  input  in_5,
  input  in_6,
  input  in_7,
  input  in_8,
  input  in_9,
  input  in_10,
  input  in_11,
  input  in_12,
  input  in_13,
  input  in_14,
  input  in_15,
  input  in_16,
  input  in_17,
  input  in_18,
  input  in_19,
  input  in_20,
  input  in_21,
  input  in_22,
  input  in_23,
  input  in_24,
  input  in_25,
  input  in_26,
  input  in_27,
  input  in_28,
  input  in_29,
  input  in_30,
  input  in_31,
  input  in_32,
  input  in_33,
  input  in_34,
  input  in_35,
  input  in_36,
  input  in_37,
  input  in_38,
  input  in_39,
  input  in_40,
  input  in_41,
  input  in_42,
  input  in_43,
  input  in_44,
  input  in_45,
  input  in_46,
  input  in_47,
  input  in_48,
  input  in_49,
  input  in_50,
  input  in_51,
  input  in_52,
  input  in_53,
  input  in_54,
  input  in_55,
  input  in_56,
  input  in_57,
  input  in_58,
  input  in_59,
  input  in_60,
  input  in_61,
  input  in_62,
  input  in_63,
  input  in_64,
  input  in_65,
  input  in_66,
  input  in_67,
  input  in_68,
  input  in_69,
  input  in_70,
  input  in_71,
  input  in_72,
  input  in_73,
  input  in_74,
  input  in_75,
  input  in_76,
  input  in_77,
  input  in_78,
  input  in_79,
  input  in_80,
  input  in_81,
  input  in_82,
  input  in_83,
  input  in_84,
  input  in_85,
  input  in_86,
  input  in_87,
  input  in_88,
  input  in_89,
  input  in_90,
  input  in_91,
  input  in_92,
  input  in_93,
  input  in_94,
  input  in_95,
  input  in_96,
  input  in_97,
  input  in_98,
  input  in_99,
  input  in_100,
  input  in_101,
  input  in_102,
  input  in_103,
  input  in_104,
  input  in_105,
  input  in_106,
  input  in_107,
  input  in_108,
  input  in_109,
  input  in_110,
  input  in_111,
  input  in_112,
  input  in_113,
  input  in_114,
  input  in_115,
  input  in_116,
  input  in_117,
  input  in_118,
  input  in_119,
  input  in_120,
  input  in_121,
  input  in_122,
  input  in_123,
  input  in_124,
  input  in_125,
  input  in_126,
  input  in_127,
  input  in_128,
  input  in_129,
  input  in_130,
  input  in_131,
  input  in_132,
  input  in_133,
  input  in_134,
  input  in_135,
  input  in_136,
  input  clk,
  input  in_138,
  input  in_139,
  input  in_140
);

  wire AC, AC_0, AC_1, AC_2, AC_3, AC_4, AC_5, AC_6, AC_7, AC_8, AC_9, AC_10, AC_11, AC_12, AC_13, AC_14,
       AC_15, ADD, add_1_s, add_2_s, add_3_s, add_4_s, add_5_s, add_6_s, add_7_s, add_8_s, add_9_s, add_10_s,
       add_11_s, add_12_s, add_13_s, add_14_s, add_15_s, add_16_s, AND, and_1_out, and_2_out, and_3_out,
       and_4_out, and_5_out, and_6_out, and_7_out, and_8_out, and_9_out, and_10_out, and_11_out, and_12_out,
       and_13_out, and_14_out, and_15_out, and_16_out, and_17_out, and_18_out, and_19_out, and_20_out,
       and_21_out, and_22_out, and_23_out, and_24_out, and_25_out, and_26_out, and_27_out, and_28_out,
       and_29_out, and_30_out, and_31_out, and_32_out, and_33_out, and_34_out, and_37_out, and_38_out,
       and_39_out, and_41_out, and_42_out, and_43_out, and_44_out, and_45_out, and_46_out, and_47_out,
       and_48_out, and_49_out, and_50_out, and_51_out, and_52_out, and_53_out, and_54_out, and_55_out,
       and_56_out, and_57_out, and_58_out, and_59_out, and_60_out, and_61_out, and_62_out, and_63_out,
       and_64_out, and_65_out, and_66_out, and_67_out, and_68_out, and_69_out, and_70_out, and_71_out,
       and_72_out, and_73_out, and_74_out, and_75_out, and_76_out, and_77_out, and_78_out, and_79_out,
       and_80_out, and_81_out, and_82_out, and_83_out, and_84_out, and_85_out, and_86_out, and_87_out,
       and_88_out, and_89_out, and_90_out, and_91_out, and_92_out, and_93_out, and_94_out, and_95_out,
       and_96_out, and_97_out, and_98_out, and_99_out, and_100_out, and_101_out, and_102_out, and_103_out,
       and_104_out, and_105_out, and_106_out, and_107_out, and_108_out, and_109_out, and_110_out,
       and_111_out, and_112_out, and_113_out, and_114_out, and_115_out, and_116_out, and_117_out,
       and_118_out, and_119_out, and_120_out, and_121_out, and_122_out, and_123_out, and_124_out,
       and_125_out, and_126_out, and_127_out, and_128_out, and_129_out, and_130_out, and_131_out,
       and_132_out, and_133_out, and_134_out, and_135_out, and_136_out, and_137_out, and_138_out,
       and_139_out, and_140_out, and_141_out, and_142_out, and_143_out, and_144_out, and_145_out,
       and_146_out, and_147_out, and_148_out, and_149_out, and_150_out, and_151_out, and_152_out,
       and_153_out, and_154_out, and_155_out, and_156_out, and_157_out, and_158_out, and_159_out,
       and_160_out, and_161_out, and_162_out, and_163_out, and_164_out, and_165_out, and_166_out,
       and_167_out, and_168_out, and_169_out, and_170_out, and_171_out, and_172_out, and_173_out,
       and_176_out, and_177_out, and_178_out, and_179_out, and_180_out, and_181_out, and_182_out,
       and_183_out, and_184_out, and_185_out, and_186_out, and_187_out, and_188_out, and_189_out,
       and_190_out, and_191_out, and_192_out, and_193_out, and_194_out, and_195_out, and_196_out,
       and_197_out, and_198_out, and_199_out, and_200_out, and_201_out, and_202_out, and_203_out,
       and_204_out, and_205_out, and_206_out, and_207_out, and_208_out, and_209_out, and_210_out,
       and_211_out, and_212_out, and_213_out, and_214_out, and_215_out, and_216_out, and_217_out,
       and_218_out, and_219_out, and_220_out, and_221_out, and_222_out, and_223_out, and_224_out,
       and_225_out, and_226_out, and_227_out, and_229_out, and_230_out, and_231_out, and_232_out,
       and_233_out, and_234_out, and_235_out, and_236_out, and_237_out, and_238_out, and_239_out,
       and_240_out, and_241_out, and_242_out, and_243_out, and_244_out, and_245_out, and_246_out,
       and_247_out, and_248_out, and_249_out, and_250_out, and_251_out, and_252_out, and_253_out,
       and_254_out, and_255_out, and_256_out, and_257_out, and_258_out, and_259_out, and_260_out,
       and_261_out, and_262_out, and_263_out, and_264_out, and_265_out, and_266_out, and_267_out,
       and_268_out, and_269_out, and_270_out, and_271_out, and_272_out, and_273_out, and_274_out,
       and_275_out, and_276_out, and_277_out, and_278_out, and_279_out, and_280_out, and_281_out,
       and_282_out, and_283_out, and_284_out, and_285_out, and_286_out, and_287_out, and_292_out,
       and_294_out, and_295_out, and_296_out, and_302_out, and_303_out, and_304_out, and_305_out,
       and_306_out, and_307_out, and_308_out, and_309_out, and_310_out, and_311_out, and_312_out,
       and_313_out, and_314_out, and_315_out, and_316_out, and_317_out, and_318_out, and_319_out,
       and_320_out, and_321_out, and_322_out, and_323_out, and_324_out, and_325_out, and_326_out,
       and_327_out, and_328_out, and_329_out, and_330_out, and_331_out, and_332_out, and_333_out,
       and_334_out, and_335_out, and_336_out, and_337_out, and_338_out, and_339_out, and_340_out,
       and_341_out, and_342_out, and_343_out, and_344_out, and_346_out, and_347_out, and_348_out,
       and_349_out, and_351_out, and_352_out, and_353_out, and_354_out, and_355_out, and_356_out,
       and_357_out, and_358_out, and_359_out, and_360_out, and_361_out, and_362_out, and_363_out,
       and_364_out, and_365_out, and_366_out, and_367_out, and_368_out, and_369_out, and_370_out,
       and_371_out, and_372_out, and_373_out, and_374_out, and_375_out, and_376_out, and_377_out,
       and_378_out, and_379_out, and_380_out, and_381_out, and_382_out, and_383_out, and_384_out,
       and_385_out, and_386_out, and_387_out, and_388_out, and_389_out, and_390_out, and_391_out,
       and_392_out, and_393_out, and_394_out, and_395_out, and_399_out, and_400_out, and_401_out,
       and_402_out, and_403_out, and_404_out, and_405_out, and_406_out, and_407_out, and_408_out,
       and_409_out, and_410_out, and_411_out, and_412_out, and_413_out, and_414_out, and_415_out,
       and_416_out, and_417_out, and_418_out, and_419_out, and_420_out, and_421_out, and_422_out,
       and_423_out, and_424_out, and_425_out, and_426_out, and_427_out, and_428_out, and_429_out,
       and_430_out, and_431_out, and_432_out, and_433_out, and_434_out, and_435_out, and_436_out,
       and_437_out, and_438_out, and_439_out, and_440_out, and_441_out, and_442_out, and_443_out,
       and_444_out, and_445_out, and_446_out, AR_0, AR_1, AR_2, AR_3, AR_4, AR_5, AR_6, AR_7, AR_8, AR_9,
       AR_10, AR_11, B_0, B_1, B_2, B_3, B_4, B_5, B_6, B_7, B_8, B_9, B_10, B_11, bus_0, bus_1, bus_2,
       bus_3, bus_4, bus_5, bus_6, bus_7, bus_8, bus_9, bus_10, bus_11, bus_12, bus_13, bus_14, bus_15, C_1,
       C_2, C_3, C_4, C_5, C_6, C_7, C_8, C_9, C_10, C_11, C_12, C_13, C_14, C_15, C_out, CLR, CLR_AR,
       CLR_PC, CLR_SC, COM, D_0, D_1, D_2, D_3, D_4, D_5, D_6, D_7, DR, DR_0, DR_1, DR_2, DR_3, DR_4, DR_5,
       DR_6, DR_7, DR_8, DR_9, DR_10, DR_11, DR_12, DR_13, DR_14, DR_15, DR_trnsfr, E, FGI, FGO, I, IEN, INC,
       INC_AR, INC_DR, INC_PC, INPR_0, INPR_1, INPR_2, INPR_3, INPR_4, INPR_5, INPR_6, INPR_7, INPR_trnsfr,
       IR_12, IR_13, IR_14, IR_15, l_0, l_1, l_2, l_3, l_4, l_5, l_6, l_7, l_8, l_9, l_10, l_11, l_12, l_13,
       l_14, l_15, LD_AC, LD_AR, LD_DR, LD_IR, LD_OUTR, LD_PC, LD_TR, mem_0, mem_1, mem_2, mem_3, mem_4,
       mem_5, mem_6, mem_7, mem_8, mem_9, mem_10, mem_11, mem_12, mem_13, mem_14, mem_15, not_1_out,
       not_2_out, not_3_out, not_4_out, not_5_out, not_6_out, not_7_out, not_8_out, not_9_out, not_10_out,
       not_11_out, not_12_out, not_13_out, not_14_out, not_15_out, not_16_out, not_17_out, not_18_out,
       not_19_out, not_20_out, not_21_out, not_22_out, not_23_out, not_24_out, not_25_out, not_26_out,
       not_27_out, not_28_out, not_29_out, not_30_out, not_31_out, not_32_out, not_33_out, not_34_out,
       not_35_out, not_36_out, not_37_out, not_38_out, not_39_out, not_40_out, not_41_out, not_42_out,
       not_43_out, not_44_out, not_45_out, not_46_out, not_47_out, not_48_out, not_49_out, not_50_out,
       not_51_out, not_52_out, not_53_out, not_54_out, not_55_out, not_56_out, not_57_out, not_58_out,
       not_59_out, not_60_out, not_61_out, not_62_out, not_63_out, not_64_out, not_65_out, not_66_out,
       not_67_out, not_68_out, not_69_out, not_70_out, not_71_out, not_72_out, or_4_out, or_5_out, or_6_out,
       or_7_out, or_8_out, or_9_out, or_10_out, or_11_out, or_12_out, or_21_out, or_22_out, or_23_out,
       or_24_out, or_25_out, or_26_out, or_27_out, or_28_out, or_33_out, or_34_out, or_35_out, or_36_out,
       or_37_out, or_38_out, or_39_out, or_40_out, or_45_out, or_46_out, or_48_out, or_49_out, or_50_out,
       or_51_out, or_52_out, or_53_out, or_54_out, or_55_out, or_60_out, or_61_out, or_62_out, or_63_out,
       or_64_out, or_65_out, or_66_out, or_67_out, or_68_out, or_69_out, or_70_out, or_71_out, or_72_out,
       or_73_out, or_74_out, or_75_out, or_76_out, or_77_out, or_78_out, or_79_out, or_80_out, or_81_out,
       or_82_out, or_83_out, or_84_out, or_85_out, or_86_out, or_87_out, or_88_out, or_89_out, or_90_out,
       or_91_out, or_92_out, or_93_out, or_94_out, or_95_out, or_96_out, or_97_out, or_98_out, or_99_out,
       or_100_out, or_101_out, or_102_out, or_103_out, or_104_out, or_105_out, or_106_out, or_107_out,
       or_108_out, or_109_out, or_110_out, or_111_out, or_112_out, or_113_out, or_114_out, or_115_out,
       or_116_out, or_117_out, or_118_out, or_119_out, or_120_out, or_121_out, or_122_out, or_123_out,
       or_124_out, or_126_out, or_127_out, or_128_out, or_129_out, or_130_out, or_131_out, or_132_out,
       or_133_out, or_134_out, or_135_out, or_136_out, or_137_out, or_138_out, or_139_out, or_140_out,
       or_141_out, or_142_out, or_143_out, or_144_out, or_145_out, or_146_out, or_147_out, or_148_out,
       or_149_out, or_150_out, or_151_out, or_152_out, or_153_out, or_155_out, or_156_out, or_158_out,
       or_159_out, or_160_out, or_161_out, or_162_out, or_163_out, or_164_out, or_165_out, or_166_out,
       or_167_out, or_168_out, or_169_out, or_170_out, or_171_out, or_172_out, or_173_out, or_174_out,
       or_175_out, or_176_out, or_177_out, or_178_out, or_179_out, or_180_out, or_181_out, or_182_out,
       or_183_out, or_184_out, or_186_out, or_187_out, or_188_out, or_189_out, or_190_out, or_191_out,
       or_192_out, or_193_out, or_194_out, or_195_out, or_196_out, or_197_out, or_198_out, or_199_out,
       or_200_out, or_201_out, or_202_out, or_203_out, or_204_out, or_205_out, or_206_out, or_207_out,
       or_208_out, or_209_out, or_210_out, or_211_out, or_212_out, or_213_out, or_214_out, or_215_out,
       or_216_out, or_217_out, or_218_out, or_219_out, or_220_out, or_221_out, or_222_out, or_223_out,
       or_224_out, or_225_out, or_226_out, or_227_out, or_228_out, or_230_out, or_231_out, or_232_out,
       or_233_out, or_235_out, or_236_out, or_237_out, or_238_out, or_239_out, or_240_out, or_241_out,
       or_242_out, OUTR_0, OUTR_1, OUTR_2, OUTR_3, OUTR_4, OUTR_5, OUTR_6, OUTR_7, p, PC_0, PC_1, PC_2, PC_3,
       PC_4, PC_5, PC_6, PC_7, PC_8, PC_9, PC_10, PC_11, R, r_t, S, S_0, S_1, S_2, SHL, SHR, T_0, T_1, T_2,
       T_3, T_4, T_5, T_6, T_7, TR_0, TR_1, TR_2, TR_3, TR_4, TR_5, TR_6, TR_7, TR_8, TR_9, TR_10, TR_11,
       TR_12, TR_13, TR_14, TR_15, x_1, x_2, x_3, x_4, x_5, x_6, x_7;
  wire [2:0] jk_ff_66_q;

  and and_1 (and_1_out, D_4, T_4);
  and and_2 (and_2_out, D_5, T_5);
  and and_3 (and_3_out, ~R, T_0);  // And
  and and_4 (and_4_out, R, T_0);
  and and_5 (and_5_out, D_3, T_4);
  and and_6 (and_6_out, p, B_10);
  or or_1 (x_1, and_1_out, and_2_out);
  or or_2 (x_2, and_3_out, and_4_out);
  or or_3 (x_4, and_5_out, and_6_out);
  and and_7 (and_7_out, DR_0, AC_0, AND);
  Add add_1 (.a(DR_0), .b(AC_0), .c_i(1'b0), .s(add_1_s), .c_o(C_1));
  and and_8 (and_8_out, DR_0, DR_trnsfr);
  and and_9 (and_9_out, INPR_0, INPR_trnsfr);
  and and_10 (and_10_out, ~AC_0, COM);  // And
  and and_11 (and_11_out, E, SHL);
  and and_12 (and_12_out, AC_2, SHR);
  and and_13 (and_13_out, DR_1, AC_1, AND);
  Add add_2 (.a(DR_1), .b(AC_1), .c_i(C_1), .s(add_2_s), .c_o(C_2));
  and and_14 (and_14_out, DR_1, DR_trnsfr);
  and and_15 (and_15_out, INPR_1, INPR_trnsfr);
  and and_16 (and_16_out, ~AC_1, COM);  // And
  and and_17 (and_17_out, AC_0, SHL);
  and and_18 (and_18_out, AC_2, SHR);
  and and_19 (and_19_out, DR_2, AC_2, AND);
  Add add_3 (.a(DR_2), .b(AC_2), .c_i(C_2), .s(add_3_s), .c_o(C_3));
  and and_20 (and_20_out, DR_2, DR_trnsfr);
  and and_21 (and_21_out, INPR_2, INPR_trnsfr);
  and and_22 (and_22_out, ~AC_2, COM);  // And
  and and_23 (and_23_out, AC_1, SHL);
  and and_24 (and_24_out, AC_3, SHR);
  and and_25 (and_25_out, DR_3, AC_3, AND);
  Add add_4 (.a(DR_3), .b(AC_3), .c_i(C_3), .s(add_4_s), .c_o(C_4));
  and and_26 (and_26_out, DR_3, DR_trnsfr);
  and and_27 (and_27_out, INPR_3, INPR_trnsfr);
  and and_28 (and_28_out, ~AC_3, COM);  // And
  and and_29 (and_29_out, AC_2, SHL);
  and and_30 (and_30_out, AC_4, SHR);
  and and_31 (and_31_out, ADD, add_1_s);
  and and_32 (and_32_out, ADD, add_2_s);
  and and_33 (and_33_out, ADD, add_3_s);
  and and_34 (and_34_out, ADD, add_4_s);
  and and_35 (x_5, ~R, T_2);  // And
  and and_36 (x_6, R, T_0);
  or or_4 (or_4_out, D_0, D_1, D_6, D_2);
  or or_5 (or_5_out, and_7_out, and_31_out, and_8_out, and_9_out);
  or or_6 (or_6_out, and_10_out, and_11_out, and_12_out);
  or or_7 (or_7_out, and_13_out, and_32_out, and_14_out, and_15_out);
  or or_8 (or_8_out, and_16_out, and_17_out, and_18_out);
  or or_9 (or_9_out, and_19_out, and_33_out, and_20_out, and_21_out);
  or or_10 (or_10_out, and_22_out, and_23_out, and_24_out);
  or or_11 (or_11_out, and_25_out, and_34_out, and_26_out, and_27_out);
  or or_12 (or_12_out, and_28_out, and_29_out, and_30_out);
  and and_37 (and_37_out, ~R, T_1);  // And
  and and_38 (and_38_out, ~D_7, I, T_3);  // And
  and and_39 (and_39_out, T_4, or_4_out);
  and and_40 (x_3, D_6, T_6);
  or or_13 (x_7, and_37_out, and_38_out, and_39_out);
  or or_14 (l_0, or_5_out, or_6_out);
  or or_15 (l_1, or_7_out, or_8_out);
  or or_16 (l_2, or_9_out, or_10_out);
  or or_17 (l_3, or_11_out, or_12_out);
  Multiplexer #(.Selector_Bits(3)) multiplexer_1 (
    .sel({AR_2, AR_1, AR_0}), .in_0(in_9), .in_1(in_25), .in_2(in_41), .in_3(in_57), .in_4(in_73),
    .in_5(in_89), .in_6(in_105), .in_7(in_121), .out(mem_0));
  Multiplexer #(.Selector_Bits(3)) multiplexer_2 (
    .sel({AR_2, AR_1, AR_0}), .in_0(in_17), .in_1(in_33), .in_2(in_49), .in_3(in_65), .in_4(in_81),
    .in_5(in_97), .in_6(in_113), .in_7(in_129), .out(mem_8));
  or or_18 (S_0, x_1, x_3, x_5, x_7);
  or or_19 (S_1, x_2, x_3, x_6, x_7);
  or or_20 (S_2, x_4, x_5, x_6, x_7);
  and and_41 (and_41_out, DR_4, AC_4, AND);
  Add add_5 (.a(DR_4), .b(AC_4), .c_i(C_4), .s(add_5_s), .c_o(C_5));
  and and_42 (and_42_out, DR_4, DR_trnsfr);
  and and_43 (and_43_out, INPR_4, INPR_trnsfr);
  and and_44 (and_44_out, ~AC_4, COM);  // And
  and and_45 (and_45_out, AC_3, SHL);
  and and_46 (and_46_out, AC_5, SHR);
  and and_47 (and_47_out, DR_5, AC_5, AND);
  Add add_6 (.a(DR_5), .b(AC_5), .c_i(C_5), .s(add_6_s), .c_o(C_6));
  and and_48 (and_48_out, DR_5, DR_trnsfr);
  and and_49 (and_49_out, INPR_5, INPR_trnsfr);
  and and_50 (and_50_out, ~AC_5, COM);  // And
  and and_51 (and_51_out, AC_4, SHL);
  and and_52 (and_52_out, AC_6, SHR);
  and and_53 (and_53_out, DR_6, AC_6, AND);
  Add add_7 (.a(DR_6), .b(AC_6), .c_i(C_6), .s(add_7_s), .c_o(C_7));
  and and_54 (and_54_out, DR_6, DR_trnsfr);
  and and_55 (and_55_out, INPR_6, INPR_trnsfr);
  and and_56 (and_56_out, ~AC_6, COM);  // And
  and and_57 (and_57_out, AC_5, SHL);
  and and_58 (and_58_out, AC_7, SHR);
  and and_59 (and_59_out, DR_7, AC_7, AND);
  Add add_8 (.a(DR_7), .b(AC_7), .c_i(C_7), .s(add_8_s), .c_o(C_8));
  and and_60 (and_60_out, DR_7, DR_trnsfr);
  and and_61 (and_61_out, INPR_7, INPR_trnsfr);
  and and_62 (and_62_out, ~AC_7, COM);  // And
  and and_63 (and_63_out, AC_6, SHL);
  and and_64 (and_64_out, AC_8, SHR);
  Multiplexer #(.Selector_Bits(3)) multiplexer_3 (
    .sel({AR_2, AR_1, AR_0}), .in_0(in_10), .in_1(in_26), .in_2(in_42), .in_3(in_58), .in_4(in_74),
    .in_5(in_90), .in_6(in_106), .in_7(in_122), .out(mem_1));
  Multiplexer #(.Selector_Bits(3)) multiplexer_4 (
    .sel({AR_2, AR_1, AR_0}), .in_0(in_18), .in_1(in_34), .in_2(in_50), .in_3(in_66), .in_4(in_82),
    .in_5(in_98), .in_6(in_114), .in_7(in_130), .out(mem_9));
  and and_65 (and_65_out, ADD, add_5_s);
  and and_66 (and_66_out, ADD, add_6_s);
  and and_67 (and_67_out, ADD, add_7_s);
  and and_68 (and_68_out, ADD, add_8_s);
  Multiplexer #(.Selector_Bits(3)) multiplexer_5 (
    .sel({S_2, S_1, S_0}), .in_0(1'b0), .in_1(AR_0), .in_2(PC_0), .in_3(DR_0), .in_4(AC_0), .in_5(B_0),
    .in_6(TR_0), .in_7(mem_0), .out(bus_0));
  Multiplexer #(.Selector_Bits(3)) multiplexer_6 (
    .sel({S_2, S_1, S_0}), .in_0(1'b0), .in_1(AR_8), .in_2(PC_8), .in_3(DR_8), .in_4(AC_8), .in_5(B_8),
    .in_6(TR_8), .in_7(mem_8), .out(bus_8));
  or or_21 (or_21_out, and_41_out, and_65_out, and_42_out, and_43_out);
  or or_22 (or_22_out, and_44_out, and_45_out, and_46_out);
  or or_23 (or_23_out, and_47_out, and_66_out, and_48_out, and_49_out);
  or or_24 (or_24_out, and_50_out, and_51_out, and_52_out);
  or or_25 (or_25_out, and_53_out, and_67_out, and_54_out, and_55_out);
  or or_26 (or_26_out, and_56_out, and_57_out, and_58_out);
  or or_27 (or_27_out, and_59_out, and_68_out, and_60_out, and_61_out);
  or or_28 (or_28_out, and_62_out, and_63_out, and_64_out);
  Multiplexer #(.Selector_Bits(3)) multiplexer_7 (
    .sel({AR_2, AR_1, AR_0}), .in_0(in_11), .in_1(in_27), .in_2(in_43), .in_3(in_59), .in_4(in_75),
    .in_5(in_91), .in_6(in_107), .in_7(in_123), .out(mem_2));
  Multiplexer #(.Selector_Bits(3)) multiplexer_8 (
    .sel({AR_2, AR_1, AR_0}), .in_0(in_19), .in_1(in_35), .in_2(in_51), .in_3(in_67), .in_4(in_83),
    .in_5(in_99), .in_6(in_115), .in_7(in_131), .out(mem_10));
  or or_29 (l_4, or_21_out, or_22_out);
  or or_30 (l_5, or_23_out, or_24_out);
  or or_31 (l_6, or_25_out, or_26_out);
  or or_32 (l_7, or_27_out, or_28_out);
  Multiplexer #(.Selector_Bits(3)) multiplexer_9 (
    .sel({S_2, S_1, S_0}), .in_0(1'b0), .in_1(AR_1), .in_2(PC_1), .in_3(DR_1), .in_4(AC_1), .in_5(B_1),
    .in_6(TR_1), .in_7(mem_1), .out(bus_1));
  Multiplexer #(.Selector_Bits(3)) multiplexer_10 (
    .sel({S_2, S_1, S_0}), .in_0(1'b0), .in_1(AR_9), .in_2(PC_9), .in_3(DR_9), .in_4(AC_9), .in_5(B_9),
    .in_6(TR_9), .in_7(mem_9), .out(bus_9));
  Multiplexer #(.Selector_Bits(3)) multiplexer_11 (
    .sel({S_2, S_1, S_0}), .in_0(1'b0), .in_1(AR_2), .in_2(PC_2), .in_3(DR_2), .in_4(AC_2), .in_5(B_2),
    .in_6(TR_2), .in_7(mem_2), .out(bus_2));
  Multiplexer #(.Selector_Bits(3)) multiplexer_12 (
    .sel({S_2, S_1, S_0}), .in_0(1'b0), .in_1(AR_10), .in_2(PC_10), .in_3(DR_10), .in_4(AC_10), .in_5(B_10),
    .in_6(TR_10), .in_7(mem_10), .out(bus_10));
  Multiplexer #(.Selector_Bits(3)) multiplexer_13 (
    .sel({AR_2, AR_1, AR_0}), .in_0(in_12), .in_1(in_28), .in_2(in_44), .in_3(in_60), .in_4(in_76),
    .in_5(in_92), .in_6(in_108), .in_7(in_124), .out(mem_3));
  Multiplexer #(.Selector_Bits(3)) multiplexer_14 (
    .sel({AR_2, AR_1, AR_0}), .in_0(in_20), .in_1(in_36), .in_2(in_52), .in_3(in_68), .in_4(in_84),
    .in_5(in_100), .in_6(in_116), .in_7(in_132), .out(mem_11));
  Add add_9 (.a(DR_8), .b(AC_8), .c_i(C_8), .s(add_9_s), .c_o(C_9));
  Add add_10 (.a(DR_9), .b(AC_9), .c_i(C_9), .s(add_10_s), .c_o(C_10));
  Add add_11 (.a(DR_10), .b(AC_10), .c_i(C_10), .s(add_11_s), .c_o(C_11));
  Add add_12 (.a(DR_11), .b(AC_11), .c_i(C_11), .s(add_12_s), .c_o(C_12));
  and and_69 (and_69_out, DR_8, AC_8, AND);
  and and_70 (and_70_out, ADD, add_9_s);
  and and_71 (and_71_out, DR_8, DR_trnsfr);
  and and_72 (and_72_out, 1'b0, INPR_trnsfr);
  and and_73 (and_73_out, ~AC_8, COM);  // And
  and and_74 (and_74_out, AC_7, SHL);
  and and_75 (and_75_out, AC_9, SHR);
  and and_76 (and_76_out, DR_9, AC_9, AND);
  and and_77 (and_77_out, ADD, add_10_s);
  and and_78 (and_78_out, DR_9, DR_trnsfr);
  and and_79 (and_79_out, 1'b0, INPR_trnsfr);
  and and_80 (and_80_out, ~AC_9, COM);  // And
  and and_81 (and_81_out, AC_8, SHL);
  and and_82 (and_82_out, AC_10, SHR);
  and and_83 (and_83_out, DR_10, AC_10, AND);
  and and_84 (and_84_out, ADD, add_11_s);
  and and_85 (and_85_out, DR_10, DR_trnsfr);
  and and_86 (and_86_out, 1'b0, INPR_trnsfr);
  and and_87 (and_87_out, ~AC_10, COM);  // And
  and and_88 (and_88_out, AC_9, SHL);
  and and_89 (and_89_out, AC_11, SHR);
  and and_90 (and_90_out, DR_11, AC_11, AND);
  and and_91 (and_91_out, ADD, add_12_s);
  and and_92 (and_92_out, DR_11, DR_trnsfr);
  and and_93 (and_93_out, 1'b0, INPR_trnsfr);
  and and_94 (and_94_out, ~AC_11, COM);  // And
  and and_95 (and_95_out, AC_10, SHL);
  and and_96 (and_96_out, AC_12, SHR);
  D_FF d_ff_1 (.D(in_1), .C(clk), .Q(INPR_0));  // open: nQ
  Multiplexer #(.Selector_Bits(3)) multiplexer_15 (
    .sel({S_2, S_1, S_0}), .in_0(1'b0), .in_1(AR_3), .in_2(PC_3), .in_3(DR_3), .in_4(AC_3), .in_5(B_3),
    .in_6(TR_3), .in_7(mem_3), .out(bus_3));
  Multiplexer #(.Selector_Bits(3)) multiplexer_16 (
    .sel({S_2, S_1, S_0}), .in_0(1'b0), .in_1(AR_0), .in_2(PC_0), .in_3(DR_11), .in_4(AC_11), .in_5(B_11),
    .in_6(TR_11), .in_7(mem_11), .out(bus_11));
  Multiplexer #(.Selector_Bits(3)) multiplexer_17 (
    .sel({AR_2, AR_1, AR_0}), .in_0(in_13), .in_1(in_29), .in_2(in_45), .in_3(in_61), .in_4(in_77),
    .in_5(in_93), .in_6(in_109), .in_7(in_125), .out(mem_4));
  Multiplexer #(.Selector_Bits(3)) multiplexer_18 (
    .sel({AR_2, AR_1, AR_0}), .in_0(in_21), .in_1(in_37), .in_2(in_53), .in_3(in_69), .in_4(in_85),
    .in_5(in_101), .in_6(in_117), .in_7(in_133), .out(mem_12));
  or or_33 (or_33_out, and_69_out, and_70_out, and_71_out, and_72_out);
  or or_34 (or_34_out, and_73_out, and_74_out, and_75_out);
  or or_35 (or_35_out, and_76_out, and_77_out, and_78_out, and_79_out);
  or or_36 (or_36_out, and_80_out, and_81_out, and_82_out);
  or or_37 (or_37_out, and_83_out, and_84_out, and_85_out, and_86_out);
  or or_38 (or_38_out, and_87_out, and_88_out, and_89_out);
  or or_39 (or_39_out, and_90_out, and_91_out, and_92_out, and_93_out);
  or or_40 (or_40_out, and_94_out, and_95_out, and_96_out);
  D_FF d_ff_2 (.D(in_2), .C(clk), .Q(INPR_1));  // open: nQ
  or or_41 (l_8, or_33_out, or_34_out);
  or or_42 (l_9, or_35_out, or_36_out);
  or or_43 (l_10, or_37_out, or_38_out);
  or or_44 (l_11, or_39_out, or_40_out);
  D_FF d_ff_3 (.D(in_3), .C(clk), .Q(INPR_2));  // open: nQ
  Multiplexer #(.Selector_Bits(3)) multiplexer_19 (
    .sel({S_2, S_1, S_0}), .in_0(1'b0), .in_1(AR_0), .in_2(PC_4), .in_3(DR_4), .in_4(AC_4), .in_5(B_4),
    .in_6(TR_4), .in_7(mem_4), .out(bus_4));
  Multiplexer #(.Selector_Bits(3)) multiplexer_20 (
    .sel({S_2, S_1, S_0}), .in_0(1'b0), .in_1(1'b0), .in_2(1'b0), .in_3(DR_12), .in_4(AC_12), .in_5(1'b0),
    .in_6(TR_12), .in_7(mem_12), .out(bus_12));
  Multiplexer #(.Selector_Bits(3)) multiplexer_21 (
    .sel({AR_2, AR_1, AR_0}), .in_0(in_14), .in_1(in_30), .in_2(in_46), .in_3(in_62), .in_4(in_78),
    .in_5(in_94), .in_6(in_110), .in_7(in_126), .out(mem_5));
  Multiplexer #(.Selector_Bits(3)) multiplexer_22 (
    .sel({AR_2, AR_1, AR_0}), .in_0(in_22), .in_1(in_38), .in_2(in_54), .in_3(in_70), .in_4(in_86),
    .in_5(in_102), .in_6(in_118), .in_7(in_134), .out(mem_13));
  D_FF d_ff_4 (.D(in_4), .C(clk), .Q(INPR_3));  // open: nQ
  D_FF d_ff_5 (.D(in_5), .C(clk), .Q(INPR_4));  // open: nQ
  Multiplexer #(.Selector_Bits(3)) multiplexer_23 (
    .sel({S_2, S_1, S_0}), .in_0(1'b0), .in_1(AR_5), .in_2(PC_5), .in_3(DR_5), .in_4(AC_5), .in_5(B_5),
    .in_6(TR_5), .in_7(mem_5), .out(bus_5));
  Multiplexer #(.Selector_Bits(3)) multiplexer_24 (
    .sel({S_2, S_1, S_0}), .in_0(1'b0), .in_1(1'b0), .in_2(1'b0), .in_3(DR_13), .in_4(AC_13), .in_5(1'b0),
    .in_6(TR_13), .in_7(mem_13), .out(bus_13));
  Add add_13 (.a(DR_12), .b(AC_12), .c_i(C_12), .s(add_13_s), .c_o(C_13));
  Add add_14 (.a(DR_13), .b(AC_13), .c_i(C_13), .s(add_14_s), .c_o(C_14));
  Add add_15 (.a(DR_14), .b(AC_14), .c_i(C_14), .s(add_15_s), .c_o(C_15));
  Add add_16 (.a(DR_15), .b(AC_15), .c_i(C_15), .s(add_16_s), .c_o(C_out));
  Multiplexer #(.Selector_Bits(3)) multiplexer_25 (
    .sel({AR_2, AR_1, AR_0}), .in_0(in_15), .in_1(in_31), .in_2(in_47), .in_3(in_63), .in_4(in_79),
    .in_5(in_95), .in_6(in_111), .in_7(in_127), .out(mem_6));
  Multiplexer #(.Selector_Bits(3)) multiplexer_26 (
    .sel({AR_2, AR_1, AR_0}), .in_0(in_23), .in_1(in_39), .in_2(in_55), .in_3(in_71), .in_4(in_87),
    .in_5(in_103), .in_6(in_119), .in_7(in_135), .out(mem_14));
  or or_45 (or_45_out, AND, ADD, DR_trnsfr, INPR_trnsfr);
  or or_46 (or_46_out, COM, SHR, SHL);
  and and_97 (and_97_out, DR_12, AC_12, AND);
  and and_98 (and_98_out, ADD, add_13_s);
  and and_99 (and_99_out, DR_12, DR_trnsfr);
  and and_100 (and_100_out, 1'b0, INPR_trnsfr);
  and and_101 (and_101_out, ~AC_12, COM);  // And
  and and_102 (and_102_out, AC_11, SHL);
  and and_103 (and_103_out, AC_13, SHR);
  and and_104 (and_104_out, DR_13, AC_13, AND);
  and and_105 (and_105_out, ADD, add_14_s);
  and and_106 (and_106_out, DR_13, DR_trnsfr);
  and and_107 (and_107_out, 1'b0, INPR_trnsfr);
  and and_108 (and_108_out, ~AC_13, COM);  // And
  and and_109 (and_109_out, AC_12, SHL);
  and and_110 (and_110_out, AC_13, SHR);
  and and_111 (and_111_out, DR_14, AC_14, AND);
  and and_112 (and_112_out, ADD, add_15_s);
  and and_113 (and_113_out, DR_14, DR_trnsfr);
  and and_114 (and_114_out, 1'b0, INPR_trnsfr);
  and and_115 (and_115_out, ~AC_14, COM);  // And
  and and_116 (and_116_out, AC_14, SHL);
  and and_117 (and_117_out, AC_15, SHR);
  and and_118 (and_118_out, DR_15, AC_15, AND);
  and and_119 (and_119_out, ADD, add_16_s);
  and and_120 (and_120_out, DR_15, DR_trnsfr);
  and and_121 (and_121_out, 1'b0, INPR_trnsfr);
  and and_122 (and_122_out, ~AC_15, COM);  // And
  and and_123 (and_123_out, AC_14, SHL);
  and and_124 (and_124_out, E, SHR);
  D_FF d_ff_6 (.D(in_6), .C(clk), .Q(INPR_5));  // open: nQ
  Multiplexer #(.Selector_Bits(3)) multiplexer_27 (
    .sel({S_2, S_1, S_0}), .in_0(1'b0), .in_1(AR_6), .in_2(PC_6), .in_3(DR_6), .in_4(AC_6), .in_5(B_6),
    .in_6(TR_6), .in_7(mem_6), .out(bus_6));
  Multiplexer #(.Selector_Bits(3)) multiplexer_28 (
    .sel({S_2, S_1, S_0}), .in_0(1'b0), .in_1(1'b0), .in_2(1'b0), .in_3(DR_14), .in_4(AC_14), .in_5(1'b0),
    .in_6(TR_14), .in_7(mem_14), .out(bus_14));
  or or_47 (LD_AC, or_45_out, or_46_out);
  D_FF d_ff_7 (.D(in_7), .C(clk), .Q(INPR_6));  // open: nQ
  or or_48 (or_48_out, and_97_out, and_98_out, and_99_out, and_100_out);
  or or_49 (or_49_out, and_101_out, and_102_out, and_103_out);
  or or_50 (or_50_out, and_104_out, and_105_out, and_106_out, and_107_out);
  or or_51 (or_51_out, and_108_out, and_109_out, and_110_out);
  or or_52 (or_52_out, and_111_out, and_112_out, and_113_out, and_114_out);
  or or_53 (or_53_out, and_115_out, and_116_out, and_117_out);
  or or_54 (or_54_out, and_118_out, and_119_out, and_120_out, and_121_out);
  or or_55 (or_55_out, and_122_out, and_123_out, and_124_out);
  Multiplexer #(.Selector_Bits(3)) multiplexer_29 (
    .sel({AR_2, AR_1, AR_0}), .in_0(in_16), .in_1(in_32), .in_2(in_48), .in_3(in_64), .in_4(in_80),
    .in_5(in_96), .in_6(in_112), .in_7(in_128), .out(mem_7));
  Multiplexer #(.Selector_Bits(3)) multiplexer_30 (
    .sel({AR_2, AR_1, AR_0}), .in_0(in_24), .in_1(in_40), .in_2(in_56), .in_3(in_72), .in_4(in_88),
    .in_5(in_104), .in_6(in_120), .in_7(in_136), .out(mem_15));
  or or_56 (l_12, or_48_out, or_49_out);
  or or_57 (l_13, or_50_out, or_51_out);
  or or_58 (l_14, or_52_out, or_53_out);
  or or_59 (l_15, or_54_out, or_55_out);
  D_FF d_ff_8 (.D(in_8), .C(clk), .Q(INPR_7));  // open: nQ
  Multiplexer #(.Selector_Bits(3)) multiplexer_31 (
    .sel({S_2, S_1, S_0}), .in_0(1'b0), .in_1(AR_7), .in_2(PC_7), .in_3(DR_7), .in_4(AC_7), .in_5(B_7),
    .in_6(TR_7), .in_7(mem_7), .out(bus_7));
  Multiplexer #(.Selector_Bits(3)) multiplexer_32 (
    .sel({S_2, S_1, S_0}), .in_0(1'b0), .in_1(1'b0), .in_2(1'b0), .in_3(DR_0), .in_4(AC_0), .in_5(1'b0),
    .in_6(TR_0), .in_7(mem_0), .out(bus_15));
  not not_1 (not_1_out, CLR);
  not not_2 (not_2_out, LD_AC);
  and and_125 (and_125_out, not_1_out, LD_AC);
  and and_126 (and_126_out, not_1_out, not_2_out, INC);
  not not_3 (not_3_out, l_0);
  not not_4 (not_4_out, l_1);
  not not_5 (not_5_out, l_2);
  not not_6 (not_6_out, l_3);
  not not_7 (not_7_out, l_4);
  not not_8 (not_8_out, l_5);
  not not_9 (not_9_out, l_6);
  not not_10 (not_10_out, l_7);
  not not_11 (not_11_out, l_8);
  not not_12 (not_12_out, l_9);
  not not_13 (not_13_out, l_10);
  not not_14 (not_14_out, l_11);
  not not_15 (not_15_out, l_12);
  not not_16 (not_16_out, l_13);
  not not_17 (not_17_out, l_14);
  not not_18 (not_18_out, l_15);
  and and_127 (and_127_out, and_125_out, l_0);
  and and_128 (and_128_out, and_125_out, not_3_out);
  and and_129 (and_129_out, and_125_out, l_1);
  and and_130 (and_130_out, and_125_out, not_4_out);
  and and_131 (and_131_out, and_125_out, l_2);
  and and_132 (and_132_out, and_125_out, not_5_out);
  and and_133 (and_133_out, and_125_out, l_3);
  and and_134 (and_134_out, and_125_out, not_6_out);
  and and_135 (and_135_out, and_125_out, l_4);
  and and_136 (and_136_out, and_125_out, not_7_out);
  and and_137 (and_137_out, and_125_out, l_5);
  and and_138 (and_138_out, and_125_out, not_8_out);
  and and_139 (and_139_out, and_125_out, l_6);
  and and_140 (and_140_out, and_125_out, not_9_out);
  and and_141 (and_141_out, and_125_out, l_7);
  and and_142 (and_142_out, and_125_out, not_10_out);
  and and_143 (and_143_out, and_125_out, l_8);
  and and_144 (and_144_out, and_125_out, not_11_out);
  and and_145 (and_145_out, and_125_out, l_9);
  and and_146 (and_146_out, and_125_out, not_12_out);
  and and_147 (and_147_out, and_125_out, l_10);
  and and_148 (and_148_out, and_125_out, not_13_out);
  and and_149 (and_149_out, and_125_out, l_11);
  and and_150 (and_150_out, and_125_out, not_14_out);
  and and_151 (and_151_out, and_125_out, l_12);
  and and_152 (and_152_out, and_125_out, not_15_out);
  and and_153 (and_153_out, and_125_out, l_13);
  and and_154 (and_154_out, and_125_out, not_16_out);
  and and_155 (and_155_out, and_125_out, l_14);
  and and_156 (and_156_out, and_125_out, not_17_out);
  and and_157 (and_157_out, and_125_out, l_15);
  and and_158 (and_158_out, and_125_out, not_18_out);
  and and_159 (and_159_out, AC_0, and_126_out);
  and and_160 (and_160_out, AC_1, and_159_out);
  and and_161 (and_161_out, AC_2, and_160_out);
  and and_162 (and_162_out, AC_3, and_161_out);
  and and_163 (and_163_out, AC_4, and_162_out);
  and and_164 (and_164_out, AC_5, and_163_out);
  and and_165 (and_165_out, AC_6, and_164_out);
  and and_166 (and_166_out, AC_7, and_165_out);
  and and_167 (and_167_out, AC_8, and_166_out);
  and and_168 (and_168_out, AC_9, and_167_out);
  and and_169 (and_169_out, AC_10, and_168_out);
  and and_170 (and_170_out, AC_11, and_169_out);
  and and_171 (and_171_out, AC_12, and_170_out);
  and and_172 (and_172_out, AC_13, and_171_out);
  and and_173 (and_173_out, AC_14, and_172_out);
  or or_60 (or_60_out, and_126_out, and_127_out);
  or or_61 (or_61_out, CLR, and_126_out, and_128_out);
  or or_62 (or_62_out, and_159_out, and_129_out);
  or or_63 (or_63_out, CLR, and_159_out, and_130_out);
  or or_64 (or_64_out, and_160_out, and_131_out);
  or or_65 (or_65_out, CLR, and_160_out, and_132_out);
  or or_66 (or_66_out, and_161_out, and_133_out);
  or or_67 (or_67_out, CLR, and_161_out, and_134_out);
  or or_68 (or_68_out, and_162_out, and_135_out);
  or or_69 (or_69_out, CLR, and_162_out, and_136_out);
  or or_70 (or_70_out, and_163_out, and_137_out);
  or or_71 (or_71_out, CLR, and_163_out, and_138_out);
  or or_72 (or_72_out, and_164_out, and_139_out);
  or or_73 (or_73_out, CLR, and_164_out, and_140_out);
  or or_74 (or_74_out, and_165_out, and_141_out);
  or or_75 (or_75_out, CLR, and_165_out, and_142_out);
  or or_76 (or_76_out, and_166_out, and_143_out);
  or or_77 (or_77_out, CLR, and_166_out, and_144_out);
  or or_78 (or_78_out, and_167_out, and_145_out);
  or or_79 (or_79_out, CLR, and_167_out, and_146_out);
  or or_80 (or_80_out, and_168_out, and_147_out);
  or or_81 (or_81_out, CLR, and_168_out, and_148_out);
  or or_82 (or_82_out, and_169_out, and_149_out);
  or or_83 (or_83_out, CLR, and_169_out, and_150_out);
  or or_84 (or_84_out, and_170_out, and_151_out);
  or or_85 (or_85_out, CLR, and_170_out, and_152_out);
  or or_86 (or_86_out, and_171_out, and_153_out);
  or or_87 (or_87_out, CLR, and_171_out, and_154_out);
  or or_88 (or_88_out, and_172_out, and_155_out);
  or or_89 (or_89_out, CLR, and_172_out, and_156_out);
  or or_90 (or_90_out, and_173_out, and_157_out);
  or or_91 (or_91_out, CLR, and_173_out, and_158_out);
  JK_FF jk_ff_1 (.J(or_60_out), .C(clk), .K(or_61_out), .Q(AC_0));  // open: nQ
  JK_FF jk_ff_2 (.J(or_62_out), .C(clk), .K(or_63_out), .Q(AC_1));  // open: nQ
  JK_FF jk_ff_3 (.J(or_64_out), .C(clk), .K(or_65_out), .Q(AC_2));  // open: nQ
  JK_FF jk_ff_4 (.J(or_66_out), .C(clk), .K(or_67_out), .Q(AC_3));  // open: nQ
  JK_FF jk_ff_5 (.J(or_68_out), .C(clk), .K(or_69_out), .Q(AC_4));  // open: nQ
  JK_FF jk_ff_6 (.J(or_70_out), .C(clk), .K(or_71_out), .Q(AC_5));  // open: nQ
  JK_FF jk_ff_7 (.J(or_72_out), .C(clk), .K(or_73_out), .Q(AC_6));  // open: nQ
  JK_FF jk_ff_8 (.J(or_74_out), .C(clk), .K(or_75_out), .Q(AC_7));  // open: nQ
  JK_FF jk_ff_9 (.J(or_76_out), .C(clk), .K(or_77_out), .Q(AC_8));  // open: nQ
  JK_FF jk_ff_10 (.J(or_78_out), .C(clk), .K(or_79_out), .Q(AC_9));  // open: nQ
  JK_FF jk_ff_11 (.J(or_80_out), .C(clk), .K(or_81_out), .Q(AC_10));  // open: nQ
  JK_FF jk_ff_12 (.J(or_82_out), .C(clk), .K(or_83_out), .Q(AC_11));  // open: nQ
  JK_FF jk_ff_13 (.J(or_84_out), .C(clk), .K(or_85_out), .Q(AC_12));  // open: nQ
  JK_FF jk_ff_14 (.J(or_86_out), .C(clk), .K(or_87_out), .Q(AC_13));  // open: nQ
  JK_FF jk_ff_15 (.J(or_88_out), .C(clk), .K(or_89_out), .Q(AC_14));  // open: nQ
  JK_FF jk_ff_16 (.J(or_90_out), .C(clk), .K(or_91_out), .Q(AC_15));  // open: nQ
  not not_19 (not_19_out, 1'b0);
  not not_20 (not_20_out, LD_DR);
  and and_174 (INC_DR, T_5, D_6);
  or or_92 (or_92_out, D_0, D_1, D_2, D_6);
  and and_175 (LD_DR, T_4, or_92_out);
  and and_176 (and_176_out, not_19_out, LD_DR);
  and and_177 (and_177_out, not_19_out, not_20_out, INC_DR);
  not not_21 (not_21_out, bus_0);
  not not_22 (not_22_out, bus_1);
  not not_23 (not_23_out, bus_2);
  not not_24 (not_24_out, bus_3);
  not not_25 (not_25_out, bus_4);
  not not_26 (not_26_out, bus_5);
  not not_27 (not_27_out, bus_6);
  not not_28 (not_28_out, bus_7);
  not not_29 (not_29_out, bus_8);
  not not_30 (not_30_out, bus_9);
  not not_31 (not_31_out, bus_10);
  not not_32 (not_32_out, bus_11);
  not not_33 (not_33_out, bus_12);
  not not_34 (not_34_out, bus_13);
  not not_35 (not_35_out, bus_14);
  not not_36 (not_36_out, bus_15);
  and and_178 (and_178_out, and_176_out, bus_0);
  and and_179 (and_179_out, and_176_out, not_21_out);
  and and_180 (and_180_out, and_176_out, bus_1);
  and and_181 (and_181_out, and_176_out, not_22_out);
  and and_182 (and_182_out, and_176_out, bus_2);
  and and_183 (and_183_out, and_176_out, not_23_out);
  and and_184 (and_184_out, and_176_out, bus_3);
  and and_185 (and_185_out, and_176_out, not_24_out);
  and and_186 (and_186_out, and_176_out, bus_4);
  and and_187 (and_187_out, and_176_out, not_25_out);
  and and_188 (and_188_out, and_176_out, bus_5);
  and and_189 (and_189_out, and_176_out, not_26_out);
  and and_190 (and_190_out, and_176_out, bus_6);
  and and_191 (and_191_out, and_176_out, not_27_out);
  and and_192 (and_192_out, and_176_out, bus_7);
  and and_193 (and_193_out, and_176_out, not_28_out);
  and and_194 (and_194_out, and_176_out, bus_8);
  and and_195 (and_195_out, and_176_out, not_29_out);
  and and_196 (and_196_out, and_176_out, bus_9);
  and and_197 (and_197_out, and_176_out, not_30_out);
  and and_198 (and_198_out, and_176_out, bus_10);
  and and_199 (and_199_out, and_176_out, not_31_out);
  and and_200 (and_200_out, and_176_out, bus_11);
  and and_201 (and_201_out, and_176_out, not_32_out);
  and and_202 (and_202_out, and_176_out, bus_12);
  and and_203 (and_203_out, and_176_out, not_33_out);
  and and_204 (and_204_out, and_176_out, bus_13);
  and and_205 (and_205_out, and_176_out, not_34_out);
  and and_206 (and_206_out, and_176_out, bus_14);
  and and_207 (and_207_out, and_176_out, not_35_out);
  and and_208 (and_208_out, and_176_out, bus_15);
  and and_209 (and_209_out, and_176_out, not_36_out);
  and and_210 (and_210_out, DR_0, and_177_out);
  and and_211 (and_211_out, DR_1, and_210_out);
  and and_212 (and_212_out, DR_2, and_211_out);
  and and_213 (and_213_out, DR_3, and_212_out);
  and and_214 (and_214_out, DR_4, and_213_out);
  and and_215 (and_215_out, DR_5, and_214_out);
  and and_216 (and_216_out, DR_6, and_215_out);
  and and_217 (and_217_out, DR_7, and_216_out);
  and and_218 (and_218_out, DR_8, and_217_out);
  and and_219 (and_219_out, DR_9, and_218_out);
  and and_220 (and_220_out, DR_10, and_219_out);
  and and_221 (and_221_out, DR_11, and_220_out);
  and and_222 (and_222_out, DR_12, and_221_out);
  and and_223 (and_223_out, DR_13, and_222_out);
  and and_224 (and_224_out, DR_14, and_223_out);
  or or_93 (or_93_out, and_177_out, and_178_out);
  or or_94 (or_94_out, 1'b0, and_177_out, and_179_out);
  or or_95 (or_95_out, and_210_out, and_180_out);
  or or_96 (or_96_out, 1'b0, and_210_out, and_181_out);
  or or_97 (or_97_out, and_211_out, and_182_out);
  or or_98 (or_98_out, 1'b0, and_211_out, and_183_out);
  or or_99 (or_99_out, and_212_out, and_184_out);
  or or_100 (or_100_out, 1'b0, and_212_out, and_185_out);
  or or_101 (or_101_out, and_213_out, and_186_out);
  or or_102 (or_102_out, 1'b0, and_213_out, and_187_out);
  or or_103 (or_103_out, and_214_out, and_188_out);
  or or_104 (or_104_out, 1'b0, and_214_out, and_189_out);
  or or_105 (or_105_out, and_215_out, and_190_out);
  or or_106 (or_106_out, 1'b0, and_215_out, and_191_out);
  or or_107 (or_107_out, and_216_out, and_192_out);
  or or_108 (or_108_out, 1'b0, and_216_out, and_193_out);
  or or_109 (or_109_out, and_217_out, and_194_out);
  or or_110 (or_110_out, 1'b0, and_217_out, and_195_out);
  or or_111 (or_111_out, and_218_out, and_196_out);
  or or_112 (or_112_out, 1'b0, and_218_out, and_197_out);
  or or_113 (or_113_out, and_219_out, and_198_out);
  or or_114 (or_114_out, 1'b0, and_219_out, and_199_out);
  or or_115 (or_115_out, and_220_out, and_200_out);
  or or_116 (or_116_out, 1'b0, and_220_out, and_201_out);
  or or_117 (or_117_out, and_221_out, and_202_out);
  or or_118 (or_118_out, 1'b0, and_221_out, and_203_out);
  or or_119 (or_119_out, and_222_out, and_204_out);
  or or_120 (or_120_out, 1'b0, and_222_out, and_205_out);
  or or_121 (or_121_out, and_223_out, and_206_out);
  or or_122 (or_122_out, 1'b0, and_223_out, and_207_out);
  or or_123 (or_123_out, and_224_out, and_208_out);
  or or_124 (or_124_out, 1'b0, and_224_out, and_209_out);
  JK_FF jk_ff_17 (.J(or_93_out), .C(clk), .K(or_94_out), .Q(DR_0));  // open: nQ
  JK_FF jk_ff_18 (.J(or_95_out), .C(clk), .K(or_96_out), .Q(DR_1));  // open: nQ
  JK_FF jk_ff_19 (.J(or_97_out), .C(clk), .K(or_98_out), .Q(DR_2));  // open: nQ
  JK_FF jk_ff_20 (.J(or_99_out), .C(clk), .K(or_100_out), .Q(DR_3));  // open: nQ
  JK_FF jk_ff_21 (.J(or_101_out), .C(clk), .K(or_102_out), .Q(DR_4));  // open: nQ
  JK_FF jk_ff_22 (.J(or_103_out), .C(clk), .K(or_104_out), .Q(DR_5));  // open: nQ
  JK_FF jk_ff_23 (.J(or_105_out), .C(clk), .K(or_106_out), .Q(DR_6));  // open: nQ
  JK_FF jk_ff_24 (.J(or_107_out), .C(clk), .K(or_108_out), .Q(DR_7));  // open: nQ
  JK_FF jk_ff_25 (.J(or_109_out), .C(clk), .K(or_110_out), .Q(DR_8));  // open: nQ
  JK_FF jk_ff_26 (.J(or_111_out), .C(clk), .K(or_112_out), .Q(DR_9));  // open: nQ
  JK_FF jk_ff_27 (.J(or_113_out), .C(clk), .K(or_114_out), .Q(DR_10));  // open: nQ
  JK_FF jk_ff_28 (.J(or_115_out), .C(clk), .K(or_116_out), .Q(DR_11));  // open: nQ
  JK_FF jk_ff_29 (.J(or_117_out), .C(clk), .K(or_118_out), .Q(DR_12));  // open: nQ
  JK_FF jk_ff_30 (.J(or_119_out), .C(clk), .K(or_120_out), .Q(DR_13));  // open: nQ
  JK_FF jk_ff_31 (.J(or_121_out), .C(clk), .K(or_122_out), .Q(DR_14));  // open: nQ
  JK_FF jk_ff_32 (.J(or_123_out), .C(clk), .K(or_124_out), .Q(DR_15));  // open: nQ
  and and_225 (and_225_out, D_1, T_5);
  and and_226 (and_226_out, T_4, D_4);
  and and_227 (and_227_out, T_5, D_5);
  and and_228 (CLR_PC, T_1, R);
  not not_37 (not_37_out, CLR_PC);
  not not_38 (not_38_out, LD_PC);
  and and_229 (and_229_out, r_t, B_8);
  and and_230 (and_230_out, and_225_out, C_out);
  and and_231 (and_231_out, and_225_out, ~C_out);  // And
  or or_125 (LD_PC, and_226_out, and_227_out);
  and and_232 (and_232_out, r_t, B_7);
  and and_233 (and_233_out, not_37_out, LD_PC);
  and and_234 (and_234_out, and_232_out, AC_0);
  and and_235 (and_235_out, and_232_out, ~AC_0);  // And
  and and_236 (and_236_out, FGO, B_9);
  and and_237 (and_237_out, FGI, B_8);
  and and_238 (and_238_out, and_229_out, E);
  or or_126 (or_126_out, and_236_out, and_237_out);
  and and_239 (and_239_out, not_37_out, not_38_out, INC_PC);
  not not_39 (not_39_out, bus_0);
  not not_40 (not_40_out, bus_1);
  not not_41 (not_41_out, bus_2);
  not not_42 (not_42_out, bus_3);
  not not_43 (not_43_out, bus_4);
  not not_44 (not_44_out, bus_5);
  not not_45 (not_45_out, bus_6);
  not not_46 (not_46_out, bus_7);
  not not_47 (not_47_out, bus_8);
  not not_48 (not_48_out, bus_9);
  not not_49 (not_49_out, bus_10);
  not not_50 (not_50_out, bus_11);
  and and_240 (and_240_out, r_t, B_6);
  and and_241 (and_241_out, and_229_out, ~E);  // And
  and and_242 (and_242_out, r_t, B_1, ~E);  // And
  and and_243 (and_243_out, r_t, B_2, ~AC);  // And
  and and_244 (and_244_out, r_t, B_3, AC_15);
  and and_245 (and_245_out, r_t, B_4, ~AC_15);  // And
  and and_246 (and_246_out, and_233_out, bus_0);
  and and_247 (and_247_out, and_233_out, not_39_out);
  and and_248 (and_248_out, and_233_out, bus_1);
  and and_249 (and_249_out, and_233_out, not_40_out);
  and and_250 (and_250_out, and_233_out, bus_2);
  and and_251 (and_251_out, and_233_out, not_41_out);
  and and_252 (and_252_out, and_233_out, bus_3);
  and and_253 (and_253_out, and_233_out, not_42_out);
  and and_254 (and_254_out, and_233_out, bus_4);
  and and_255 (and_255_out, and_233_out, not_43_out);
  and and_256 (and_256_out, and_233_out, bus_5);
  and and_257 (and_257_out, and_233_out, not_44_out);
  and and_258 (and_258_out, and_233_out, bus_6);
  and and_259 (and_259_out, and_233_out, not_45_out);
  and and_260 (and_260_out, and_233_out, bus_7);
  and and_261 (and_261_out, and_233_out, not_46_out);
  and and_262 (and_262_out, and_233_out, bus_8);
  and and_263 (and_263_out, and_233_out, not_47_out);
  and and_264 (and_264_out, and_233_out, bus_9);
  and and_265 (and_265_out, and_233_out, not_48_out);
  and and_266 (and_266_out, and_233_out, bus_10);
  and and_267 (and_267_out, and_233_out, not_49_out);
  and and_268 (and_268_out, and_233_out, bus_11);
  and and_269 (and_269_out, and_233_out, not_50_out);
  and and_270 (and_270_out, and_240_out, AC_15);
  and and_271 (and_271_out, and_240_out, ~AC_15);  // And
  and and_272 (and_272_out, r_t, B_10);
  and and_273 (and_273_out, D_6, T_6, ~DR);  // And
  and and_274 (and_274_out, PC_0, and_239_out);
  and and_275 (and_275_out, PC_1, and_274_out);
  and and_276 (and_276_out, PC_2, and_275_out);
  and and_277 (and_277_out, PC_3, and_276_out);
  and and_278 (and_278_out, PC_4, and_277_out);
  and and_279 (and_279_out, PC_5, and_278_out);
  and and_280 (and_280_out, PC_6, and_279_out);
  and and_281 (and_281_out, PC_7, and_280_out);
  and and_282 (and_282_out, PC_8, and_281_out);
  and and_283 (and_283_out, PC_9, and_282_out);
  and and_284 (and_284_out, PC_10, and_283_out);
  or or_127 (or_127_out, and_270_out, and_234_out, and_241_out, and_230_out);
  or or_128 (or_128_out, and_235_out, and_271_out, and_238_out, and_231_out, and_272_out);
  or or_129 (or_129_out, and_242_out, and_243_out, and_245_out, and_244_out);
  and and_285 (and_285_out, p, or_126_out);
  or or_130 (or_130_out, and_239_out, and_246_out);
  or or_131 (or_131_out, CLR_PC, and_239_out, and_247_out);
  or or_132 (or_132_out, and_274_out, and_248_out);
  or or_133 (or_133_out, CLR_PC, and_274_out, and_249_out);
  or or_134 (or_134_out, and_275_out, and_250_out);
  or or_135 (or_135_out, CLR_PC, and_275_out, and_251_out);
  or or_136 (or_136_out, and_276_out, and_252_out);
  or or_137 (or_137_out, CLR_PC, and_276_out, and_253_out);
  or or_138 (or_138_out, and_277_out, and_254_out);
  or or_139 (or_139_out, CLR_PC, and_277_out, and_255_out);
  or or_140 (or_140_out, and_278_out, and_256_out);
  or or_141 (or_141_out, CLR_PC, and_278_out, and_257_out);
  or or_142 (or_142_out, and_279_out, and_258_out);
  or or_143 (or_143_out, CLR_PC, and_279_out, and_259_out);
  or or_144 (or_144_out, and_280_out, and_260_out);
  or or_145 (or_145_out, CLR_PC, and_280_out, and_261_out);
  or or_146 (or_146_out, and_281_out, and_262_out);
  or or_147 (or_147_out, CLR_PC, and_281_out, and_263_out);
  or or_148 (or_148_out, and_282_out, and_264_out);
  or or_149 (or_149_out, CLR_PC, and_282_out, and_265_out);
  or or_150 (or_150_out, and_283_out, and_266_out);
  or or_151 (or_151_out, CLR_PC, and_283_out, and_267_out);
  or or_152 (or_152_out, and_284_out, and_268_out);
  or or_153 (or_153_out, CLR_PC, and_284_out, and_269_out);
  and and_286 (and_286_out, T_2, R);
  and and_287 (and_287_out, T_1, ~R);  // And
  JK_FF jk_ff_33 (.J(or_127_out), .C(clk), .K(or_128_out), .Q(E));  // open: nQ
  or or_154 (INC_PC, or_129_out, and_285_out, and_273_out, and_286_out, and_287_out);
  JK_FF jk_ff_34 (.J(or_130_out), .C(clk), .K(or_131_out), .Q(PC_0));  // open: nQ
  JK_FF jk_ff_35 (.J(or_132_out), .C(clk), .K(or_133_out), .Q(PC_1));  // open: nQ
  JK_FF jk_ff_36 (.J(or_134_out), .C(clk), .K(or_135_out), .Q(PC_2));  // open: nQ
  JK_FF jk_ff_37 (.J(or_136_out), .C(clk), .K(or_137_out), .Q(PC_3));  // open: nQ
  JK_FF jk_ff_38 (.J(or_138_out), .C(clk), .K(or_139_out), .Q(PC_4));  // open: nQ
  JK_FF jk_ff_39 (.J(or_140_out), .C(clk), .K(or_141_out), .Q(PC_5));  // open: nQ
  JK_FF jk_ff_40 (.J(or_142_out), .C(clk), .K(or_143_out), .Q(PC_6));  // open: nQ
  JK_FF jk_ff_41 (.J(or_144_out), .C(clk), .K(or_145_out), .Q(PC_7));  // open: nQ
  JK_FF jk_ff_42 (.J(or_146_out), .C(clk), .K(or_147_out), .Q(PC_8));  // open: nQ
  JK_FF jk_ff_43 (.J(or_148_out), .C(clk), .K(or_149_out), .Q(PC_9));  // open: nQ
  JK_FF jk_ff_44 (.J(or_150_out), .C(clk), .K(or_151_out), .Q(PC_10));  // open: nQ
  JK_FF jk_ff_45 (.J(or_152_out), .C(clk), .K(or_153_out), .Q(PC_11));  // open: nQ
  and and_288 (ADD, T_5, D_1);
  and and_289 (AND, T_5, D_0);
  and and_290 (DR_trnsfr, D_2, T_5);
  and and_291 (INPR_trnsfr, p, B_11);
  and and_292 (and_292_out, r_t, B_0);
  or or_155 (or_155_out, FGO, FGI);
  JK_FF jk_ff_46 (.J(in_140), .C(clk), .K(and_292_out), .Q(S));  // open: nQ
  and and_293 (INC_AR, T_4, D_5);
  not not_51 (not_51_out, CLR_AR);
  not not_52 (not_52_out, LD_AR);
  and and_294 (and_294_out, ~T_0, ~T_1, ~T_2, IEN, or_155_out);  // And
  and and_295 (and_295_out, not_51_out, LD_AR);
  and and_296 (and_296_out, R, T_2);
  and and_297 (COM, r_t, B_9);
  and and_298 (SHR, r_t, B_7);
  and and_299 (SHL, r_t, B_6);
  and and_300 (INC, r_t, B_5);
  and and_301 (CLR, r_t, B_11);
  JK_FF jk_ff_47 (.J(and_294_out), .C(clk), .K(and_296_out), .Q(R));  // open: nQ
  and and_302 (and_302_out, p, B_10);
  or or_156 (or_156_out, T_0, T_2);
  and and_303 (and_303_out, not_51_out, not_52_out, INC_AR);
  JK_FF jk_ff_48 (.J(in_138), .C(clk), .K(and_302_out), .Q(FGO));  // open: nQ
  and and_304 (and_304_out, or_156_out, ~R);  // And
  and and_305 (and_305_out, I, ~D_7, T_3);  // And
  and and_306 (and_306_out, and_295_out, bus_0);
  and and_307 (and_307_out, and_295_out, not_53_out);
  not not_53 (not_53_out, bus_0);
  and and_308 (and_308_out, and_295_out, bus_1);
  and and_309 (and_309_out, and_295_out, not_54_out);
  not not_54 (not_54_out, bus_1);
  and and_310 (and_310_out, and_295_out, bus_2);
  and and_311 (and_311_out, and_295_out, not_55_out);
  not not_55 (not_55_out, bus_2);
  and and_312 (and_312_out, and_295_out, bus_3);
  and and_313 (and_313_out, and_295_out, not_56_out);
  not not_56 (not_56_out, bus_3);
  and and_314 (and_314_out, and_295_out, bus_4);
  and and_315 (and_315_out, and_295_out, not_57_out);
  not not_57 (not_57_out, bus_4);
  and and_316 (and_316_out, and_295_out, bus_5);
  and and_317 (and_317_out, and_295_out, not_58_out);
  not not_58 (not_58_out, bus_5);
  and and_318 (and_318_out, and_295_out, bus_6);
  and and_319 (and_319_out, and_295_out, not_59_out);
  not not_59 (not_59_out, bus_6);
  and and_320 (and_320_out, and_295_out, bus_7);
  and and_321 (and_321_out, and_295_out, not_60_out);
  not not_60 (not_60_out, bus_7);
  and and_322 (and_322_out, and_295_out, bus_8);
  and and_323 (and_323_out, and_295_out, not_61_out);
  not not_61 (not_61_out, bus_8);
  and and_324 (and_324_out, and_295_out, bus_9);
  and and_325 (and_325_out, and_295_out, not_62_out);
  not not_62 (not_62_out, bus_9);
  and and_326 (and_326_out, and_295_out, bus_10);
  and and_327 (and_327_out, and_295_out, not_63_out);
  not not_63 (not_63_out, bus_10);
  and and_328 (and_328_out, and_295_out, bus_11);
  and and_329 (and_329_out, and_295_out, not_64_out);
  not not_64 (not_64_out, bus_11);
  or or_157 (LD_AR, and_304_out, and_305_out);
  and and_330 (and_330_out, ~R, T_2);  // And
  and and_331 (and_331_out, AR_0, and_303_out);
  and and_332 (and_332_out, AR_1, and_331_out);
  and and_333 (and_333_out, AR_2, and_332_out);
  and and_334 (and_334_out, AR_3, and_333_out);
  and and_335 (and_335_out, AR_4, and_334_out);
  and and_336 (and_336_out, AR_5, and_335_out);
  and and_337 (and_337_out, AR_6, and_336_out);
  and and_338 (and_338_out, AR_7, and_337_out);
  and and_339 (and_339_out, AR_8, and_338_out);
  and and_340 (and_340_out, AR_9, and_339_out);
  and and_341 (and_341_out, AR_10, and_340_out);
  and and_342 (and_342_out, and_330_out, IR_15);
  and and_343 (and_343_out, and_330_out, IR_15);
  and and_344 (and_344_out, p, B_11);
  or or_158 (or_158_out, and_303_out, and_306_out);
  or or_159 (or_159_out, CLR_AR, and_303_out, and_307_out);
  or or_160 (or_160_out, and_331_out, and_308_out);
  or or_161 (or_161_out, CLR_AR, and_331_out, and_309_out);
  or or_162 (or_162_out, and_332_out, and_310_out);
  or or_163 (or_163_out, CLR_AR, and_332_out, and_311_out);
  or or_164 (or_164_out, and_333_out, and_312_out);
  or or_165 (or_165_out, CLR_AR, and_333_out, and_313_out);
  or or_166 (or_166_out, and_334_out, and_314_out);
  or or_167 (or_167_out, CLR_AR, and_334_out, and_315_out);
  or or_168 (or_168_out, and_335_out, and_316_out);
  or or_169 (or_169_out, CLR_AR, and_335_out, and_317_out);
  or or_170 (or_170_out, and_336_out, and_318_out);
  or or_171 (or_171_out, CLR_AR, and_336_out, and_319_out);
  or or_172 (or_172_out, and_337_out, and_320_out);
  or or_173 (or_173_out, CLR_AR, and_337_out, and_321_out);
  or or_174 (or_174_out, and_338_out, and_322_out);
  or or_175 (or_175_out, CLR_AR, and_338_out, and_323_out);
  or or_176 (or_176_out, and_339_out, and_324_out);
  or or_177 (or_177_out, CLR_AR, and_339_out, and_325_out);
  or or_178 (or_178_out, and_340_out, and_326_out);
  or or_179 (or_179_out, CLR_AR, and_340_out, and_327_out);
  or or_180 (or_180_out, and_341_out, and_328_out);
  or or_181 (or_181_out, CLR_AR, and_341_out, and_329_out);
  JK_FF jk_ff_49 (.J(and_342_out), .C(clk), .K(and_343_out), .Q(I));  // open: nQ
  JK_FF jk_ff_50 (.J(in_139), .C(clk), .K(and_344_out), .Q(FGI));  // open: nQ
  and and_345 (CLR_AR, T_0, R);
  JK_FF jk_ff_51 (.J(or_158_out), .C(clk), .K(or_159_out), .Q(AR_0));  // open: nQ
  JK_FF jk_ff_52 (.J(or_160_out), .C(clk), .K(or_161_out), .Q(AR_1));  // open: nQ
  JK_FF jk_ff_53 (.J(or_162_out), .C(clk), .K(or_163_out), .Q(AR_2));  // open: nQ
  JK_FF jk_ff_54 (.J(or_164_out), .C(clk), .K(or_165_out), .Q(AR_3));  // open: nQ
  JK_FF jk_ff_55 (.J(or_166_out), .C(clk), .K(or_167_out), .Q(AR_4));  // open: nQ
  JK_FF jk_ff_56 (.J(or_168_out), .C(clk), .K(or_169_out), .Q(AR_5));  // open: nQ
  JK_FF jk_ff_57 (.J(or_170_out), .C(clk), .K(or_171_out), .Q(AR_6));  // open: nQ
  JK_FF jk_ff_58 (.J(or_172_out), .C(clk), .K(or_173_out), .Q(AR_7));  // open: nQ
  JK_FF jk_ff_59 (.J(or_174_out), .C(clk), .K(or_175_out), .Q(AR_8));  // open: nQ
  JK_FF jk_ff_60 (.J(or_176_out), .C(clk), .K(or_177_out), .Q(AR_9));  // open: nQ
  JK_FF jk_ff_61 (.J(or_178_out), .C(clk), .K(or_179_out), .Q(AR_10));  // open: nQ
  JK_FF jk_ff_62 (.J(or_180_out), .C(clk), .K(or_181_out), .Q(AR_11));  // open: nQ
  or or_182 (or_182_out, D_0, D_1, D_2, D_5);
  not not_65 (not_65_out, LD_IR);
  or or_183 (or_183_out, D_3, D_4);
  and and_346 (and_346_out, R, T_2);
  or or_184 (or_184_out, p, r_t);
  and and_347 (and_347_out, T_4, or_183_out);
  and and_348 (and_348_out, T_5, or_182_out);
  and and_349 (and_349_out, T_6, D_6);
  and and_350 (LD_IR, ~R, T_1);  // And
  not not_66 (not_66_out, CLR_SC);
  not not_67 (not_67_out, 1'b0);
  or or_185 (CLR_SC, and_346_out, or_184_out, and_347_out, and_348_out, and_349_out);
  Demultiplexer #(.Selector_Bits(3)) demultiplexer_1 (
    .sel({IR_14, IR_13, IR_12}), .in(1'b1), .out_0(D_0), .out_1(D_1), .out_2(D_2), .out_3(D_3), .out_4(D_4),
    .out_5(D_5), .out_6(D_6), .out_7(D_7));
  and and_351 (and_351_out, not_66_out, 1'b0);
  and and_352 (and_352_out, B_0, not_65_out);
  and and_353 (and_353_out, bus_0, LD_IR);
  and and_354 (and_354_out, B_1, not_65_out);
  and and_355 (and_355_out, bus_1, LD_IR);
  and and_356 (and_356_out, B_2, not_65_out);
  and and_357 (and_357_out, bus_2, LD_IR);
  and and_358 (and_358_out, B_3, not_65_out);
  and and_359 (and_359_out, bus_3, LD_IR);
  and and_360 (and_360_out, B_4, not_65_out);
  and and_361 (and_361_out, bus_4, LD_IR);
  and and_362 (and_362_out, B_5, not_65_out);
  and and_363 (and_363_out, bus_5, LD_IR);
  and and_364 (and_364_out, B_6, not_65_out);
  and and_365 (and_365_out, bus_6, LD_IR);
  and and_366 (and_366_out, B_7, not_65_out);
  and and_367 (and_367_out, bus_7, LD_IR);
  and and_368 (and_368_out, B_8, not_65_out);
  and and_369 (and_369_out, bus_8, LD_IR);
  and and_370 (and_370_out, B_9, not_65_out);
  and and_371 (and_371_out, bus_9, LD_IR);
  and and_372 (and_372_out, B_10, not_65_out);
  and and_373 (and_373_out, bus_10, LD_IR);
  and and_374 (and_374_out, B_11, not_65_out);
  and and_375 (and_375_out, bus_11, LD_IR);
  and and_376 (and_376_out, IR_12, not_65_out);
  and and_377 (and_377_out, bus_12, LD_IR);
  and and_378 (and_378_out, IR_13, not_65_out);
  and and_379 (and_379_out, bus_13, LD_IR);
  and and_380 (and_380_out, IR_14, not_65_out);
  and and_381 (and_381_out, bus_14, LD_IR);
  and and_382 (and_382_out, IR_15, not_65_out);
  and and_383 (and_383_out, bus_15, LD_IR);
  or or_186 (or_186_out, and_352_out, and_353_out);
  or or_187 (or_187_out, and_354_out, and_355_out);
  or or_188 (or_188_out, and_356_out, and_357_out);
  or or_189 (or_189_out, and_358_out, and_359_out);
  or or_190 (or_190_out, and_360_out, and_361_out);
  or or_191 (or_191_out, and_362_out, and_363_out);
  or or_192 (or_192_out, and_364_out, and_365_out);
  or or_193 (or_193_out, and_366_out, and_367_out);
  or or_194 (or_194_out, and_368_out, and_369_out);
  or or_195 (or_195_out, and_370_out, and_371_out);
  or or_196 (or_196_out, and_372_out, and_373_out);
  or or_197 (or_197_out, and_374_out, and_375_out);
  or or_198 (or_198_out, and_376_out, and_377_out);
  or or_199 (or_199_out, and_378_out, and_379_out);
  or or_200 (or_200_out, and_380_out, and_381_out);
  or or_201 (or_201_out, and_382_out, and_383_out);
  and and_384 (and_384_out, not_66_out, not_67_out, 1'b1);
  not not_68 (not_68_out, 1'b0);
  not not_69 (not_69_out, 1'b0);
  not not_70 (not_70_out, 1'b0);
  and and_385 (and_385_out, p, B_7);
  and and_386 (and_386_out, p, B_6);
  and and_387 (and_387_out, R, T_2);
  and and_388 (and_388_out, and_351_out, 1'b0);
  and and_389 (and_389_out, and_351_out, not_68_out);
  and and_390 (and_390_out, and_351_out, 1'b0);
  and and_391 (and_391_out, and_351_out, not_69_out);
  and and_392 (and_392_out, and_351_out, 1'b0);
  and and_393 (and_393_out, and_351_out, not_70_out);
  D_FF d_ff_9 (.D(or_186_out), .C(clk), .Q(B_0));  // open: nQ
  D_FF d_ff_10 (.D(or_187_out), .C(clk), .Q(B_1));  // open: nQ
  D_FF d_ff_11 (.D(or_188_out), .C(clk), .Q(B_2));  // open: nQ
  D_FF d_ff_12 (.D(or_189_out), .C(clk), .Q(B_3));  // open: nQ
  D_FF d_ff_13 (.D(or_190_out), .C(clk), .Q(B_4));  // open: nQ
  D_FF d_ff_14 (.D(or_191_out), .C(clk), .Q(B_5));  // open: nQ
  D_FF d_ff_15 (.D(or_192_out), .C(clk), .Q(B_6));  // open: nQ
  D_FF d_ff_16 (.D(or_193_out), .C(clk), .Q(B_7));  // open: nQ
  D_FF d_ff_17 (.D(or_194_out), .C(clk), .Q(B_8));  // open: nQ
  D_FF d_ff_18 (.D(or_195_out), .C(clk), .Q(B_9));  // open: nQ
  D_FF d_ff_19 (.D(or_196_out), .C(clk), .Q(B_10));  // open: nQ
  D_FF d_ff_20 (.D(or_197_out), .C(clk), .Q(B_11));  // open: nQ
  D_FF d_ff_21 (.D(or_198_out), .C(clk), .Q(IR_12));  // open: nQ
  D_FF d_ff_22 (.D(or_199_out), .C(clk), .Q(IR_13));  // open: nQ
  D_FF d_ff_23 (.D(or_200_out), .C(clk), .Q(IR_14));  // open: nQ
  D_FF d_ff_24 (.D(or_201_out), .C(clk), .Q(IR_15));  // open: nQ
  or or_202 (or_202_out, and_386_out, and_387_out);
  JK_FF jk_ff_63 (.J(and_385_out), .C(clk), .K(or_202_out), .Q(IEN));  // open: nQ
  and and_394 (and_394_out, jk_ff_66_q[0], and_384_out);
  and and_395 (and_395_out, jk_ff_66_q[1], and_394_out);
  or or_203 (or_203_out, and_384_out, and_388_out);
  or or_204 (or_204_out, CLR_SC, and_384_out, and_389_out);
  or or_205 (or_205_out, and_394_out, and_390_out);
  or or_206 (or_206_out, CLR_SC, and_394_out, and_391_out);
  or or_207 (or_207_out, and_395_out, and_392_out);
  or or_208 (or_208_out, CLR_SC, and_395_out, and_393_out);
  not not_71 (not_71_out, LD_TR);
  JK_FF jk_ff_64 (.J(or_203_out), .C(clk), .K(or_204_out), .Q(jk_ff_66_q[0]));  // open: nQ
  JK_FF jk_ff_65 (.J(or_205_out), .C(clk), .K(or_206_out), .Q(jk_ff_66_q[1]));  // open: nQ
  JK_FF jk_ff_66 (.J(or_207_out), .C(clk), .K(or_208_out), .Q(jk_ff_66_q[2]));  // open: nQ
  and and_396 (LD_TR, R, T_0);
  and and_397 (r_t, D_7, ~I, T_3);  // And
  and and_398 (p, D_7, I, T_3);
  Demultiplexer #(.Selector_Bits(3)) demultiplexer_2 (
    .sel(jk_ff_66_q), .in(1'b1), .out_0(T_0), .out_1(T_1), .out_2(T_2), .out_3(T_3), .out_4(T_4),
    .out_5(T_5), .out_6(T_6), .out_7(T_7));
  and and_399 (and_399_out, TR_0, not_71_out);
  and and_400 (and_400_out, bus_0, LD_TR);
  and and_401 (and_401_out, TR_1, not_71_out);
  and and_402 (and_402_out, bus_1, LD_TR);
  and and_403 (and_403_out, TR_2, not_71_out);
  and and_404 (and_404_out, bus_2, LD_TR);
  and and_405 (and_405_out, TR_3, not_71_out);
  and and_406 (and_406_out, bus_3, LD_TR);
  and and_407 (and_407_out, TR_4, not_71_out);
  and and_408 (and_408_out, bus_4, LD_TR);
  and and_409 (and_409_out, TR_5, not_71_out);
  and and_410 (and_410_out, bus_5, LD_TR);
  and and_411 (and_411_out, TR_6, not_71_out);
  and and_412 (and_412_out, bus_6, LD_TR);
  and and_413 (and_413_out, TR_7, not_71_out);
  and and_414 (and_414_out, bus_7, LD_TR);
  and and_415 (and_415_out, TR_8, not_71_out);
  and and_416 (and_416_out, bus_8, LD_TR);
  and and_417 (and_417_out, TR_9, not_71_out);
  and and_418 (and_418_out, bus_9, LD_TR);
  and and_419 (and_419_out, TR_10, not_71_out);
  and and_420 (and_420_out, bus_10, LD_TR);
  and and_421 (and_421_out, TR_11, not_71_out);
  and and_422 (and_422_out, bus_11, LD_TR);
  and and_423 (and_423_out, TR_12, not_71_out);
  and and_424 (and_424_out, bus_12, LD_TR);
  and and_425 (and_425_out, TR_13, not_71_out);
  and and_426 (and_426_out, bus_13, LD_TR);
  and and_427 (and_427_out, TR_14, not_71_out);
  and and_428 (and_428_out, bus_14, LD_TR);
  and and_429 (and_429_out, TR_15, not_71_out);
  and and_430 (and_430_out, bus_15, LD_TR);
  or or_209 (or_209_out, and_399_out, and_400_out);
  or or_210 (or_210_out, and_401_out, and_402_out);
  or or_211 (or_211_out, and_403_out, and_404_out);
  or or_212 (or_212_out, and_405_out, and_406_out);
  or or_213 (or_213_out, and_407_out, and_408_out);
  or or_214 (or_214_out, and_409_out, and_410_out);
  or or_215 (or_215_out, and_411_out, and_412_out);
  or or_216 (or_216_out, and_413_out, and_414_out);
  or or_217 (or_217_out, and_415_out, and_416_out);
  or or_218 (or_218_out, and_417_out, and_418_out);
  or or_219 (or_219_out, and_419_out, and_420_out);
  or or_220 (or_220_out, and_421_out, and_422_out);
  or or_221 (or_221_out, and_423_out, and_424_out);
  or or_222 (or_222_out, and_425_out, and_426_out);
  or or_223 (or_223_out, and_427_out, and_428_out);
  or or_224 (or_224_out, and_429_out, and_430_out);
  D_FF d_ff_25 (.D(or_209_out), .C(clk), .Q(TR_0));  // open: nQ
  D_FF d_ff_26 (.D(or_210_out), .C(clk), .Q(TR_1));  // open: nQ
  D_FF d_ff_27 (.D(or_211_out), .C(clk), .Q(TR_2));  // open: nQ
  D_FF d_ff_28 (.D(or_212_out), .C(clk), .Q(TR_3));  // open: nQ
  D_FF d_ff_29 (.D(or_213_out), .C(clk), .Q(TR_4));  // open: nQ
  D_FF d_ff_30 (.D(or_214_out), .C(clk), .Q(TR_5));  // open: nQ
  D_FF d_ff_31 (.D(or_215_out), .C(clk), .Q(TR_6));  // open: nQ
  D_FF d_ff_32 (.D(or_216_out), .C(clk), .Q(TR_7));  // open: nQ
  D_FF d_ff_33 (.D(or_217_out), .C(clk), .Q(TR_8));  // open: nQ
  D_FF d_ff_34 (.D(or_218_out), .C(clk), .Q(TR_9));  // open: nQ
  D_FF d_ff_35 (.D(or_219_out), .C(clk), .Q(TR_10));  // open: nQ
  D_FF d_ff_36 (.D(or_220_out), .C(clk), .Q(TR_11));  // open: nQ
  D_FF d_ff_37 (.D(or_221_out), .C(clk), .Q(TR_12));  // open: nQ
  D_FF d_ff_38 (.D(or_222_out), .C(clk), .Q(TR_13));  // open: nQ
  D_FF d_ff_39 (.D(or_223_out), .C(clk), .Q(TR_14));  // open: nQ
  D_FF d_ff_40 (.D(or_224_out), .C(clk), .Q(TR_15));  // open: nQ
  or or_225 (or_225_out, AC_0, AC_2, AC_2, AC_3);
  or or_226 (or_226_out, AC_4, AC_5, AC_6, AC_7);
  or or_227 (or_227_out, AC_8, AC_9, AC_10, AC_12);
  or or_228 (or_228_out, AC_11, AC_13, AC_14, AC_15);
  not not_72 (not_72_out, LD_OUTR);
  or or_229 (AC, or_225_out, or_226_out, or_227_out, or_228_out);
  or or_230 (or_230_out, DR_0, DR_1, DR_2, DR_3);
  or or_231 (or_231_out, DR_4, DR_5, DR_6, DR_7);
  or or_232 (or_232_out, DR_8, DR_9, DR_10, DR_12);
  or or_233 (or_233_out, DR_11, DR_13, DR_14, DR_15);
  and and_431 (and_431_out, OUTR_0, not_72_out);
  and and_432 (and_432_out, bus_0, LD_OUTR);
  and and_433 (and_433_out, OUTR_1, not_72_out);
  and and_434 (and_434_out, bus_1, LD_OUTR);
  and and_435 (and_435_out, OUTR_2, not_72_out);
  and and_436 (and_436_out, bus_2, LD_OUTR);
  and and_437 (and_437_out, OUTR_3, not_72_out);
  and and_438 (and_438_out, bus_3, LD_OUTR);
  and and_439 (and_439_out, OUTR_4, not_72_out);
  and and_440 (and_440_out, bus_4, LD_OUTR);
  and and_441 (and_441_out, OUTR_5, not_72_out);
  and and_442 (and_442_out, bus_5, LD_OUTR);
  and and_443 (and_443_out, OUTR_6, not_72_out);
  and and_444 (and_444_out, bus_6, LD_OUTR);
  and and_445 (and_445_out, OUTR_7, not_72_out);
  and and_446 (and_446_out, bus_7, LD_OUTR);
  and and_447 (LD_OUTR, p, B_10);
  or or_234 (DR, or_230_out, or_231_out, or_232_out, or_233_out);
  or or_235 (or_235_out, and_431_out, and_432_out);
  or or_236 (or_236_out, and_433_out, and_434_out);
  or or_237 (or_237_out, and_435_out, and_436_out);
  or or_238 (or_238_out, and_437_out, and_438_out);
  or or_239 (or_239_out, and_439_out, and_440_out);
  or or_240 (or_240_out, and_441_out, and_442_out);
  or or_241 (or_241_out, and_443_out, and_444_out);
  or or_242 (or_242_out, and_445_out, and_446_out);
  D_FF d_ff_41 (.D(or_235_out), .C(clk), .Q(OUTR_0));  // open: nQ
  D_FF d_ff_42 (.D(or_236_out), .C(clk), .Q(OUTR_1));  // open: nQ
  D_FF d_ff_43 (.D(or_237_out), .C(clk), .Q(OUTR_2));  // open: nQ
  D_FF d_ff_44 (.D(or_238_out), .C(clk), .Q(OUTR_3));  // open: nQ
  D_FF d_ff_45 (.D(or_239_out), .C(clk), .Q(OUTR_4));  // open: nQ
  D_FF d_ff_46 (.D(or_240_out), .C(clk), .Q(OUTR_5));  // open: nQ
  D_FF d_ff_47 (.D(or_241_out), .C(clk), .Q(OUTR_6));  // open: nQ
  D_FF d_ff_48 (.D(or_242_out), .C(clk), .Q(OUTR_7));  // open: nQ

  // Other names for the same wires on the sheet: C = clk; CLR_AC = CLR; ext_0 = in_1; ext_1 = in_2; ext_2 = in_3;
  //   ext_3 = in_4; ext_4 = in_5; ext_5 = in_6; ext_6 = in_7; ext_7 = in_8; ext_100 = in_138; ext_101 = in_139;
  //   ext_102 = in_140; INC_AC = INC; IR_0 = B_0; IR_1 = B_1; IR_2 = B_2; IR_3 = B_3; IR_4 = B_4; IR_5 = B_5;
  //   IR_6 = B_6; IR_7 = B_7; IR_8 = B_8; IR_9 = B_9; IR_10 = B_10; IR_11 = B_11; word0_0 = in_9; word0_1 = in_10;
  //   word0_2 = in_11; word0_3 = in_12; word0_4 = in_13; word0_5 = in_14; word0_6 = in_15; word0_7 = in_16;
  //   word0_8 = in_17; word0_9 = in_18; word0_10 = in_19; word0_11 = in_20; word0_12 = in_21; word0_13 = in_22;
  //   word0_14 = in_23; word0_15 = in_24; word1_0 = in_25; word1_1 = in_26; word1_2 = in_27; word1_3 = in_28;
  //   word1_4 = in_29; word1_5 = in_30; word1_6 = in_31; word1_7 = in_32; word1_8 = in_33; word1_9 = in_34;
  //   word1_10 = in_35; word1_11 = in_36; word1_12 = in_37; word1_13 = in_38; word1_14 = in_39; word1_15 = in_40;
  //   word2_0 = in_41; word2_1 = in_42; word2_2 = in_43; word2_3 = in_44; word2_4 = in_45; word2_5 = in_46;
  //   word2_6 = in_47; word2_7 = in_48; word2_8 = in_49; word2_9 = in_50; word2_10 = in_51; word2_11 = in_52;
  //   word2_12 = in_53; word2_13 = in_54; word2_14 = in_55; word2_15 = in_56; word3_0 = in_57; word3_1 = in_58;
  //   word3_2 = in_59; word3_3 = in_60; word3_4 = in_61; word3_5 = in_62; word3_6 = in_63; word3_7 = in_64;
  //   word3_8 = in_65; word3_9 = in_66; word3_10 = in_67; word3_11 = in_68; word3_12 = in_69; word3_13 = in_70;
  //   word3_14 = in_71; word3_15 = in_72; word4_0 = in_73; word4_1 = in_74; word4_2 = in_75; word4_3 = in_76;
  //   word4_4 = in_77; word4_5 = in_78; word4_6 = in_79; word4_7 = in_80; word4_8 = in_81; word4_9 = in_82;
  //   word4_10 = in_83; word4_11 = in_84; word4_12 = in_85; word4_13 = in_86; word4_14 = in_87; word4_15 = in_88;
  //   word5_0 = in_89; word5_1 = in_90; word5_2 = in_91; word5_3 = in_92; word5_4 = in_93; word5_5 = in_94;
  //   word5_6 = in_95; word5_7 = in_96; word5_8 = in_97; word5_9 = in_98; word5_10 = in_99; word5_11 = in_100;
  //   word5_12 = in_101; word5_13 = in_102; word5_14 = in_103; word5_15 = in_104; word6_0 = in_105; word6_1 = in_106;
  //   word6_2 = in_107; word6_3 = in_108; word6_4 = in_109; word6_5 = in_110; word6_6 = in_111; word6_7 = in_112;
  //   word6_8 = in_113; word6_9 = in_114; word6_10 = in_115; word6_11 = in_116; word6_12 = in_117; word6_13 = in_118;
  //   word6_14 = in_119; word6_15 = in_120; word7_0 = in_121; word7_1 = in_122; word7_2 = in_123; word7_3 = in_124;
  //   word7_4 = in_125; word7_5 = in_126; word7_6 = in_127; word7_7 = in_128; word7_8 = in_129; word7_9 = in_130;
  //   word7_10 = in_131; word7_11 = in_132; word7_12 = in_133; word7_13 = in_134; word7_14 = in_135;
  //   word7_15 = in_136

  // Notes on the sheet:
  //   in_18: default 1
  //   in_21: default 1
  //   in_22: default 1
  //   in_23: default 1
  //   Bus Encoding Logic
  //   Select AR
  //   Select PC
  //   Select AC
  //   16x Adder & Logic Circuits
  //   Select IR
  //   Select TR
  //   Select memory
  //   M[AR]
  //   Select DR
  //   Bus
  //   INPR
  //   Accumulator Pins
  //   AC
  //   DR
  //   E
  //   PC Pins
  //   PC
  //   Accumulator Functions
  //   S
  //   AR Pins
  //   AR
  //   R
  //   FGO
  //   I
  //   FGI
  //   Decoding
  //   SC
  //   IR
  //   D0-7
  //   IEN
  //   TR
  //   r | p
  //   Clock
  //   T0-7
  //   AC != 0
  //   OUTR
  //   DR != 1
endmodule
