// Digital circuit multiplier.dig as structural Verilog
module multiplier (
  input  C,
  input  C_2,
  input  C_3,
  input  C_4,
  input  C_5,
  input  C_6,
  output T0,
  output T1,
  output T2,
  output T3,
  output T4,
  output T5,
  output T6,
  output A0,
  output A1,
  output A2,
  output A3,
  output A4,
  output A5,
  output A6,
  output A7
);

  wire add_1_c_o, add_1_s, add_2_c_o, add_2_s, add_3_c_o, add_3_s, add_4_c_o, add_4_s, add_5_c_o, add_5_s,
       add_6_c_o, add_6_s, add_7_c_o, add_7_s, and_1_out, and_2_out, and_3_out, and_4_out, and_5_out,
       and_6_out, and_7_out, and_8_out, and_9_out, and_10_out, and_11_out, and_12_out, and_13_out,
       and_14_out, and_15_out, and_16_out, and_17_out, and_18_out, d_ff_1_q, d_ff_2_q, d_ff_3_q, d_ff_4_q,
       d_ff_5_q, d_ff_16_q, d_ff_19_q, d_ff_22_q, d_ff_23_q, d_ff_24_q, multiplexer_1_out, nand_1_out,
       not_1_out, or_1_out, or_2_out, or_3_out;
  wire [2:0] t_ff_2_q;

  D_FF d_ff_1 (.D(1'b1), .C(C), .Q(d_ff_1_q));  // open: nQ
  D_FF d_ff_2 (.D(1'b1), .C(C), .Q(d_ff_2_q));  // open: nQ
  xor xor_1 (A7, d_ff_5_q, d_ff_16_q);
  D_FF d_ff_3 (.D(1'b1), .C(C), .Q(d_ff_3_q));  // open: nQ
  D_FF d_ff_4 (.D(1'b1), .C(C), .Q(d_ff_4_q));  // open: nQ
  D_FF d_ff_5 (.D(add_1_c_o), .C(C_6), .Q(d_ff_5_q));  // open: nQ
  Add add_1 (.a(A6), .b(and_2_out), .c_i(add_2_c_o), .s(add_1_s), .c_o(add_1_c_o));
  and and_1 (and_1_out, T5, not_1_out);
  D_FF d_ff_6 (.D(and_1_out), .C(C_3), .Q(T6));  // open: nQ
  and and_2 (and_2_out, multiplexer_1_out, T6);
  D_FF d_ff_7 (.D(add_1_s), .C(C_6), .Q(A6));  // open: nQ
  D_FF d_ff_8 (.D(and_4_out), .C(C_3), .Q(T5));  // open: nQ
  and and_3 (and_3_out, multiplexer_1_out, T5);
  Add add_2 (.a(A5), .b(and_3_out), .c_i(add_3_c_o), .s(add_2_s), .c_o(add_2_c_o));
  D_FF d_ff_9 (.D(add_2_s), .C(C_6), .Q(A5));  // open: nQ
  and and_4 (and_4_out, T4, not_1_out);
  Add add_3 (.a(A4), .b(and_5_out), .c_i(add_4_c_o), .s(add_3_s), .c_o(add_3_c_o));
  D_FF d_ff_10 (.D(and_6_out), .C(C_3), .Q(T4));  // open: nQ
  and and_5 (and_5_out, multiplexer_1_out, T4);
  D_FF d_ff_11 (.D(add_3_s), .C(C_6), .Q(A4));  // open: nQ
  and and_6 (and_6_out, T3, not_1_out);
  Add add_4 (.a(A3), .b(and_8_out), .c_i(add_5_c_o), .s(add_4_s), .c_o(add_4_c_o));
  and and_7 (and_7_out, d_ff_1_q, nand_1_out);
  or or_1 (or_1_out, and_9_out, and_7_out);
  D_FF d_ff_12 (.D(or_1_out), .C(C_3), .Q(T3));  // open: nQ
  and and_8 (and_8_out, multiplexer_1_out, T3);
  D_FF d_ff_13 (.D(add_4_s), .C(C_6), .Q(A3));  // open: nQ
  T_FF t_ff_1 (.T(1'b1), .C(C_2), .Q(t_ff_2_q[0]));  // open: nQ
  and and_9 (and_9_out, T2, not_1_out);
  Add add_5 (.a(A2), .b(and_11_out), .c_i(add_6_c_o), .s(add_5_s), .c_o(add_5_c_o));
  and and_10 (and_10_out, d_ff_2_q, nand_1_out);
  or or_2 (or_2_out, and_12_out, and_10_out);
  D_FF d_ff_14 (.D(or_2_out), .C(C_3), .Q(T2));  // open: nQ
  and and_11 (and_11_out, multiplexer_1_out, T2);
  D_FF d_ff_15 (.D(add_5_s), .C(C_6), .Q(A2));  // open: nQ
  D_FF d_ff_16 (.D(1'b0), .C(C_5), .Q(d_ff_16_q));  // open: nQ
  T_FF t_ff_2 (.T(t_ff_2_q[0]), .C(C_2), .Q(t_ff_2_q[1]));  // open: nQ
  and and_12 (and_12_out, T1, not_1_out);
  and and_13 (and_13_out, multiplexer_1_out, T1);
  Add add_6 (.a(A1), .b(and_13_out), .c_i(add_7_c_o), .s(add_6_s), .c_o(add_6_c_o));
  D_FF d_ff_17 (.D(add_6_s), .C(C_6), .Q(A1));  // open: nQ
  and and_14 (and_14_out, t_ff_2_q[0], t_ff_2_q[1]);
  and and_15 (and_15_out, d_ff_3_q, nand_1_out);
  or or_3 (or_3_out, and_16_out, and_15_out);
  D_FF d_ff_18 (.D(or_3_out), .C(C_3), .Q(T1));  // open: nQ
  Add add_7 (.a(A0), .b(and_17_out), .c_i(1'b0), .s(add_7_s), .c_o(add_7_c_o));
  D_FF d_ff_19 (.D(1'b1), .C(C_5), .Q(d_ff_19_q));  // open: nQ
  T_FF t_ff_3 (.T(and_14_out), .C(C_2), .Q(t_ff_2_q[2]));  // open: nQ
  and and_16 (and_16_out, T0, not_1_out);
  D_FF d_ff_20 (.D(and_18_out), .C(C_3), .Q(T0));  // open: nQ
  and and_17 (and_17_out, multiplexer_1_out, T0);
  D_FF d_ff_21 (.D(add_7_s), .C(C_6), .Q(A0));  // open: nQ
  D_FF d_ff_22 (.D(1'b0), .C(C_5), .Q(d_ff_22_q));  // open: nQ
  and and_18 (and_18_out, d_ff_4_q, nand_1_out);
  not not_1 (not_1_out, nand_1_out);
  D_FF d_ff_23 (.D(1'b1), .C(C_5), .Q(d_ff_23_q));  // open: nQ
  nand nand_1 (nand_1_out, d_ff_24_q, d_ff_24_q);
  D_FF d_ff_24 (.D(1'b1), .C(C_4), .Q(d_ff_24_q));  // open: nQ
  Multiplexer #(.Selector_Bits(3)) multiplexer_1 (
    .sel(t_ff_2_q), .in_0(1'b0), .in_1(d_ff_23_q), .in_2(d_ff_22_q), .in_3(d_ff_19_q), .in_4(d_ff_16_q),
    .in_5(1'b0), .in_6(1'b0), .in_7(1'b0), .out(multiplexer_1_out));

  // Notes on the sheet:
  //   Theoretically, this XOR on the right should 
  //   not be needeed at this point because the 
  //   rest of the calculations work out perfectly.
  //   In practice, it is required because if the
  //   multiplicand's MSB is high, the final bit
  //   seems to become 0, regardless of what
  //   value the multiplicand is.
  //   The addition of this XOR fixes it to the
  //   best of my knowledge
  //   Multiplier
  //   This is where temp gets added to answer IF
  //   the 'active bit' of the multiplicand (i.e bit in
  //   selection as we go from right to left) is one.
  //   If not, no addition occurs (but shifting takes
  //   place regardless).
  //   Answer
  //   AddIfOne
  //   Temp
  //   If the input is high, bits are loaded
  //   into the right-most 4 bits of the shifter.
  //   Else, they are shifted left once per clock.
  //   In tandem with the 'loader' module, this
  //   makes it so that the first cycle is used for
  //   loading purposes.
  //   Active Bit Index Selection
  //   This is a 3 bit synchronous up counter
  //   that is piped into the mux as the selector
  //   bits to check the value of the multiplicand
  //   at the requested index. This is important
  //   so we can set the addition flag to 'off'
  //   when the value at that index is 0.
  //   Multiplicand
  //   The wire atop this text box 
  //   works as the 'shouldAdd' 
  //   flag. Refer to the AddIfOne 
  //   rectangle for a detailed
  //   explanation.
  //   This is where the final answer is kept.
  //   Values from the temp register are added
  //   to it and then put back in here.
  //   Like so: Answer += temp.
  //   Loader
  //   This module above outputs active 
  //   high for the first clock cycle, but 
  //   low for every cycle after that, making
  //   it perfect as the flag set for our 'temp'
  //   register which is first supposed to load
  //   the bits from the 'multiplier', and then 
  //   shift them left.
  //   Mux
  //   This multiplexer is used to check the value of the 
  //   multiplicand at 'active bit index' (selector bit)
  //   This 'active bit index' is a value used to shift the 
  //   'temp' register left that many times.
  //   The value of the 'active' bit is then used to determine 
  //   whether the contents of the left shift register
  //   should be added to the answer or not.
  //   Why did I use an 8:1 mux?
  //   &
  //   Potential Scaling
  //   Since in the 'temp' register, we're 'wasting' the very
  //   first clock cycle (since we use that time loading the
  //   multiplier into temp), we had to introduce this delay
  //   to start iterating through the multiplicand's bits one
  //   clock cycle late.
  //   An additional benefit of this approach is that, for the 4
  //   extra, unecessary shifts at the end, the 'shouldAdd' flag
  //   (i.e mux output) will already be zero.
  //   Additionally, this is very easy to scale up to higher degree
  //   multipliers. E.g 16-input-4-selection pins for a multiplier of
  //   8 bits, so on and so forth.
endmodule
